// Logisim project s-mips.circ as structural Verilog: 20 circuits, main circuit S-MIPS Board
module S_MIPS_Board (
  input  DESHABILITAR_DISPATCHER,
  output halt
);

  wire button_1_out, CLK, CS, d_ff_1_q, LCLR, LoadRAM, LoadRAMOn, LW, R_R_W, R_W, ram_dispatcher_1_finished,
       RCS, Reset_out, RST, TTY_EN;
  wire [2:0] KDB;
  wire [3:0] LMask, Mask, ram_1_read_time, ram_1_write_time, RMask;
  wire [6:0] KDB_DATA, TTY_DATA;
  wire [15:0] Addr, LAddr, RAddr;
  wire [31:0] I0, I1, I2, I3, LData, ram_1_data_out_0, ram_1_data_out_1, ram_1_data_out_2, ram_1_data_out_3,
       RI0, RI1, RI2, RI3;

  TTY #(.rows(25), .cols(80)) tty_1 (.data(TTY_DATA), .clk(CLK), .we(TTY_EN), .clr(RST));
  not not_1 (LoadRAMOn, ram_dispatcher_1_finished);
  RAM_Dispatcher ram_dispatcher_1 (
    .WriteTime(ram_1_write_time), .Clock(CLK), .Data(LData), .Address(LAddr), .Mask(LMask),
    .Finished(ram_dispatcher_1_finished), .Write(LW), .CLR(LCLR));
  Keyboard #(.buflen(64)) keyboard_1 (.clk(CLK), .re(KDB[0]), .avail(KDB[2]), .data(KDB_DATA));  // open: clr
  RAM ram_1 (
    .Address(RAddr), .Data_Out_0(ram_1_data_out_0), .Data_Out_1(ram_1_data_out_1),
    .Data_Out_2(ram_1_data_out_2), .Data_Out_3(ram_1_data_out_3), .Data_In_0(RI0), .Data_In_1(RI1),
    .Data_In_2(RI2), .Data_In_3(RI3), .Mask(RMask), .nRead_Write(R_R_W), .Chip_Select(RCS),
    .Read_Time(ram_1_read_time), .Reset(button_1_out), .Write_Time(ram_1_write_time));
  Button button_1 (.out(button_1_out));
  D_Flip_Flop d_ff_1 (.clk(CLK), .D(1'b1), .Q(d_ff_1_q), .reset(Reset_out));  // open: Qn, preset, en
  Button Reset (.out(Reset_out));
  S_MIPS s_mips_1 (
    .Kbd_Enable(KDB[0]), .Address(Addr), .Kbd_Clear(KDB[1]), .Kbd_Available(KDB[2]), .RAM_In_0(I0),
    .Kbd_ASCII_Data(KDB_DATA), .RAM_In_1(I1), .TTY_Enable(TTY_EN), .RAM_In_2(I2), .RAM_In_3(I3),
    .TTY_ASCII_Data(TTY_DATA), .RAM_Out_0(ram_1_data_out_0), .RAM_Out_1(ram_1_data_out_1), .out_19(halt),
    .RAM_Out_2(ram_1_data_out_2), .RAM_Out_3(ram_1_data_out_3), .Mask(Mask), .Read_Time(ram_1_read_time),
    .Write_Time(ram_1_write_time), .nRead_Write(R_W), .Chip_Select(CS), .Reset(RST), .Clock(CLK));
  D_Flip_Flop d_ff_2 (.clk(CLK), .D(d_ff_1_q), .Qn(LCLR), .reset(Reset_out));  // open: Q, preset, en
  or or_1 (RST, LCLR, LoadRAM);
  Clock clock_1 (.out(CLK));
  Multiplexer #(.width(32), .enable("false")) multiplexer_1 (.in0(I0), .in1(LData), .out(RI0), .sel(LoadRAM));
  Multiplexer #(.width(32), .enable("false")) multiplexer_2 (.in0(I1), .in1(LData), .out(RI1), .sel(LoadRAM));
  Multiplexer #(.width(32), .enable("false")) multiplexer_3 (.in0(I2), .in1(LData), .out(RI2), .sel(LoadRAM));
  Multiplexer #(.width(32), .enable("false")) multiplexer_4 (.in0(I3), .in1(LData), .out(RI3), .sel(LoadRAM));
  and and_1 (LoadRAM, ~DESHABILITAR_DISPATCHER, LoadRAMOn);  // AND_Gate
  Multiplexer #(.width(16), .enable("false")) multiplexer_5 (.in0(Addr), .in1(LAddr), .out(RAddr), .sel(LoadRAM));
  Multiplexer #(.width(4), .enable("false")) multiplexer_6 (.in0(Mask), .in1(LMask), .out(RMask), .sel(LoadRAM));
  Multiplexer #(.enable("false")) multiplexer_7 (.in0(CS), .in1(LW), .out(RCS), .sel(LoadRAM));
  Multiplexer #(.enable("false")) multiplexer_8 (.in0(R_W), .in1(LW), .out(R_R_W), .sel(LoadRAM));

  // Notes on the sheet:
  //   NO MODIFICAR
  //   Keyboard
endmodule

module RAM (
  input  [15:0] Address,
  input  [31:0] Data_In_0,
  input  [31:0] Data_In_1,
  input  [31:0] Data_In_2,
  input  [31:0] Data_In_3,
  input  [3:0] Mask,
  input  nRead_Write,
  input  Chip_Select,
  input  Reset,
  output [31:0] Data_Out_0,
  output [31:0] Data_Out_1,
  output [31:0] Data_Out_2,
  output [31:0] Data_Out_3,
  output [3:0] Read_Time,
  output [3:0] Write_Time
);

  wire and_2_out, and_3_out, and_4_out, and_5_out, and_6_out, and_7_out, and_8_out, and_9_out, Changed, CLK,
       comparator_2_eq, comparator_3_eq, comparator_4_eq, comparator_5_eq, comparator_6_eq, Count,
       demultiplexer_3_out0, Idle, Idle_q, Load, Load0, Load1, nand_1_out, or_1_out, or_2_out, or_3_out,
       or_4_out, or_5_out, or_6_out, or_7_out, or_8_out, or_9_out, or_10_out, Proc_q, Update_Mem, Zero_Time;
  wire [3:0] counter_1_q, multiplexer_1_out, subtractor_1_out;
  wire [31:0] register_1_q, register_2_q, register_3_q, register_4_q, register_5_q;

  // Probe on 4'b0011
  // Probe on 4'b0010
  Multiplexer #(.width(4), .enable("false")) multiplexer_1 (
    .in0(4'b0011), .in1(4'b0010), .out(multiplexer_1_out), .sel(nRead_Write));
  or or_1 (or_1_out, Idle, Update_Mem);
  or or_2 (or_2_out, ~Chip_Select, Reset);  // OR_Gate
  Subtractor #(.width(4)) subtractor_1 (.a(multiplexer_1_out), .b(4'b0010), .out(subtractor_1_out));  // open: bin, bout
  Demultiplexer #(.enable("false")) demultiplexer_1 (.out0(Idle), .out1(Load0), .in(Idle_q), .sel(Changed));
  D_Flip_Flop u_Idle (.clk(CLK), .D(or_1_out), .Q(Idle_q), .preset(or_2_out));  // open: Qn, en, reset
  // Probe on counter_1_q
  Counter #(.width(4), .max('hf)) counter_1 (
    .load(Load), .D(subtractor_1_out), .count(Count), .Q(counter_1_q), .clk(CLK), .clr(or_3_out));  // open: carry
  or or_3 (or_3_out, ~Chip_Select, Reset);  // OR_Gate
  Comparator #(.width(4), .mode("unsigned")) comparator_1 (
    .a(4'b0000), .b(counter_1_q), .eq(Zero_Time));  // open: gt, lt
  or or_4 (or_4_out, Count, Load0, Load1);
  Register #(.width(32)) register_1 (.D(Data_In_0), .en(Chip_Select), .Q(register_1_q), .clk(CLK), .clr(or_5_out));
  or or_5 (or_5_out, ~Chip_Select, Reset);  // OR_Gate
  Register #(.width(32)) register_2 (.D(Data_In_1), .en(Chip_Select), .Q(register_2_q), .clk(CLK), .clr(or_6_out));
  or or_6 (or_6_out, ~Chip_Select, Reset);  // OR_Gate
  Register #(.width(32)) register_3 (.D(Data_In_2), .en(Chip_Select), .Q(register_3_q), .clk(CLK), .clr(or_7_out));
  or or_7 (or_7_out, ~Chip_Select, Reset);  // OR_Gate
  Register #(.width(32)) register_4 (.D(Data_In_3), .en(Chip_Select), .Q(register_4_q), .clk(CLK), .clr(or_8_out));
  or or_8 (or_8_out, ~Chip_Select, Reset);  // OR_Gate
  Register #(.width(32)) register_5 (
    .D({{11{1'b1}}, nRead_Write, Mask, Address}), .en(Chip_Select), .Q(register_5_q), .clk(CLK),
    .clr(or_9_out));
  or or_9 (or_9_out, ~Chip_Select, Reset);  // OR_Gate
  D_Flip_Flop Proc (.clk(CLK), .D(or_4_out), .Q(Proc_q), .reset(or_10_out));  // open: Qn, preset, en
  or or_10 (or_10_out, ~Chip_Select, Reset);  // OR_Gate
  Demultiplexer #(.enable("false")) demultiplexer_2 (
    .out0(Count), .out1(Update_Mem), .in(demultiplexer_3_out0), .sel(Zero_Time));
  Demultiplexer #(.enable("false")) demultiplexer_3 (
    .out0(demultiplexer_3_out0), .out1(Load1), .in(Proc_q), .sel(Changed));
  Clock clock_1 (.out(CLK));
  Comparator #(.width(32)) comparator_2 (.a(register_1_q), .b(Data_In_0), .eq(comparator_2_eq));  // open: gt, lt
  Comparator #(.width(32)) comparator_3 (.a(register_2_q), .b(Data_In_1), .eq(comparator_3_eq));  // open: gt, lt
  Comparator #(.width(32)) comparator_4 (.a(register_3_q), .b(Data_In_2), .eq(comparator_4_eq));  // open: gt, lt
  Comparator #(.width(32)) comparator_5 (.a(register_4_q), .b(Data_In_3), .eq(comparator_5_eq));  // open: gt, lt
  Comparator #(.width(32)) comparator_6 (
    .a(register_5_q), .b({{11{1'b1}}, nRead_Write, Mask, Address}), .eq(comparator_6_eq));  // open: gt, lt
  nand nand_1 (nand_1_out, comparator_6_eq, comparator_2_eq, comparator_3_eq, comparator_4_eq, comparator_5_eq);
  and and_1 (Changed, nand_1_out, Chip_Select);
  or or_11 (Load, Count, Load1, Load0);
  and and_2 (and_2_out, Mask[0], Update_Mem, nRead_Write);
  and and_3 (and_3_out, Mask[1], Update_Mem, nRead_Write);
  and and_4 (and_4_out, Mask[2], Update_Mem, nRead_Write);
  and and_5 (and_5_out, Mask[3], Update_Mem, nRead_Write);
  RAM_part #(.addrWidth(16), .dataWidth(32), .bus("separate")) ram_1 (
    .addr(Address), .din(Data_In_0), .data(Data_Out_0), .str(and_2_out), .sel(Chip_Select), .clk(CLK),
    .ld(and_6_out), .clr(Reset));
  and and_6 (and_6_out, ~nRead_Write, Idle);  // AND_Gate
  RAM_part #(.addrWidth(16), .dataWidth(32), .bus("separate")) ram_2 (
    .addr(Address), .din(Data_In_1), .data(Data_Out_1), .str(and_3_out), .sel(Chip_Select), .clk(CLK),
    .ld(and_7_out), .clr(Reset));
  and and_7 (and_7_out, ~nRead_Write, Idle);  // AND_Gate
  RAM_part #(.addrWidth(16), .dataWidth(32), .bus("separate")) ram_3 (
    .addr(Address), .din(Data_In_2), .data(Data_Out_2), .str(and_4_out), .sel(Chip_Select), .clk(CLK),
    .ld(and_8_out), .clr(Reset));
  and and_8 (and_8_out, ~nRead_Write, Idle);  // AND_Gate
  RAM_part #(.addrWidth(16), .dataWidth(32), .bus("separate")) ram_4 (
    .addr(Address), .din(Data_In_3), .data(Data_Out_3), .str(and_5_out), .sel(Chip_Select), .clk(CLK),
    .ld(and_9_out), .clr(Reset));
  and and_9 (and_9_out, ~nRead_Write, Idle);  // AND_Gate

  assign Read_Time = 4'b0011;
  assign Write_Time = 4'b0010;

  // Other names for the same wires on the sheet: M0 = Mask[0]; M1 = Mask[1]; M2 = Mask[2]; M3 = Mask[3];
  //   RW = nRead_Write; CLR = Reset; CS = Chip_Select; Load2 = Count

  // Notes on the sheet:
  //   NO MODIFICAR
  //   excepto quizás los valores RT y WT
  //   BANK0
  //   BANK1
  //   BANK2
  //   BANK3
endmodule

module S_MIPS (
  input  [3:0] Read_Time,
  input  [31:0] RAM_Out_0,
  input  [3:0] Write_Time,
  input  Kbd_Available,
  input  [31:0] RAM_Out_1,
  input  [6:0] Kbd_ASCII_Data,
  input  [31:0] RAM_Out_2,
  input  Reset,
  input  Clock,
  input  [31:0] RAM_Out_3,
  output [15:0] Address,
  output [31:0] RAM_In_0,
  output [3:0] Mask,
  output [31:0] RAM_In_1,
  output Kbd_Enable,
  output Kbd_Clear,
  output [31:0] RAM_In_2,
  output TTY_Enable,
  output out_19,
  output [6:0] TTY_ASCII_Data,
  output [31:0] RAM_In_3,
  output nRead_Write,
  output Chip_Select
);

  wire DA_S, Hit, Load_inst, Logical_Op, lw, or_1_out, PC_Enable, pop, push, push_end, R_Miss, RW_RAM;
  wire [1:0] ALU_SB, Bank, S_Adress;
  wire [2:0] Branch_Op, DATA_S;
  wire [3:0] ALU_Op;
  wire [5:0] Func_Code, Op_Code;
  wire [31:0] Adress, Cache_Out, RAM_Data;

  Control_Unit control_unit_1 (
    .in_1(Op_Code), .in_2(Read_Time), .in_3(Clock), .in_5(Func_Code), .in_6(Write_Time), .in_7(Reset),
    .out_11(out_19), .out_12(ALU_Op), .out_13(Kbd_Enable), .out_14(Load_inst), .Salidas(DATA_S),
    .out_16(RW_RAM), .out_17(TTY_Enable), .out_18(pop), .out_9(push), .out_19(PC_Enable),
    .out_20(Logical_Op), .out_21(DA_S), .out_22(S_Adress), .out_23(Branch_Op), .out_24(ALU_SB),
    .out_25(Chip_Select), .out_26(nRead_Write), .in_4(R_Miss), .out_10(lw), .out_8(push_end));
  RAM_Manager ram_manager_1 (
    .in_1(RAM_Out_0), .in_2(RAM_Out_1), .in_3(Adress), .in_8(Clock), .in_9(Reset), .in_5(RAM_Out_2),
    .in_6(RAM_Out_3), .out_10(Address), .out_11(Mask), .out_12(RAM_Data), .out_13(Bank), .in_7(Cache_Out),
    .in_4(Hit));
  Data_Path data_path_1 (
    .in_1(nRead_Write), .in_2(DA_S), .in_3(DATA_S), .in_4(Logical_Op), .in_5(S_Adress), .in_6(ALU_Op),
    .in_7(ALU_SB), .in_8(Branch_Op), .in_10(PC_Enable), .in_11(RAM_Data), .in_12(Load_inst),
    .in_13(Kbd_ASCII_Data), .in_14(Kbd_Available), .in_15(Reset), .in_18(Clock), .out_19(Op_Code),
    .out_20(Adress), .out_21({RAM_In_0[7:0], RAM_In_0[15:8], RAM_In_0[23:16], RAM_In_0[31:24]}),
    .out_22(Func_Code), .out_23(TTY_ASCII_Data), .in_16(pop), .in_17(push), .in_9(push_end));
  Cache cache_1 (
    .in_1(Clock), .in_3(Reset), .in_7(Address), .in_5(Bank), .in_2(RW_RAM),
    .in_6({RAM_In_0[7:0], RAM_In_0[15:8], RAM_In_0[23:16], RAM_In_0[31:24]}), .out_9(Hit),
    .out_10(Cache_Out), .in_4(or_1_out), .out_8(R_Miss));
  or or_1 (or_1_out, lw, pop);

  assign Kbd_Clear = Reset;
  assign RAM_In_1 = RAM_In_0;
  assign RAM_In_2 = RAM_In_0;
  assign RAM_In_3 = RAM_In_0;

  // Other names for the same wires on the sheet: CLK = Clock; CS = Chip_Select; KBD_AVAIL = Kbd_Available;
  //   CLR = Reset; KBD_CLR = Reset; KBD_DATA[6:0] = Kbd_ASCII_Data; R_W = nRead_Write; RAM_A[15:0] = Address;
  //   RAM_INPUT_0[31:0] = RAM_In_0; RAM_INPUT_1[31:0] = RAM_In_0; RAM_INPUT_2[31:0] = RAM_In_0;
  //   RAM_INPUT_3[31:0] = RAM_In_0; Value[31:0] = {RAM_In_0[7:0], RAM_In_0[15:8], RAM_In_0[23:16], RAM_In_0[31:24]};
  //   RAM_MASK[3:0] = Mask; RAM_OUTPUT_0[31:0] = RAM_Out_0; RAM_OUTPUT_1[31:0] = RAM_Out_1;
  //   RAM_OUTPUT_2[31:0] = RAM_Out_2; RAM_OUTPUT_3[31:0] = RAM_Out_3; STOP = out_19; TTY_DATA[6:0] = TTY_ASCII_Data

  // Notes on the sheet:
  //   DATA FROM RAM
  //   Entradas
  //   RAM TIMING
  //   KEYBOARD
  //   SEQUENCING
  //   DATA TO RAM
  //   Salidas
  //   RAM ADDRESS
  //   DATA WRITE MASK
  //   KEYBOARD
  //   TTY
  //   RAM CONTROL
endmodule

module RAM_Dispatcher (
  input  [3:0] WriteTime,
  input  Clock,
  input  CLR,
  output [31:0] Data,
  output [15:0] Address,
  output [3:0] Mask,
  output Finished,
  output Write
);

  wire demultiplexer_2_out1, demultiplexer_3_out1, End, IDLE_q, IncAddr, Load, or_1_out, or_2_out, While_q,
       WriteEnd;
  wire [3:0] counter_1_q;
  wire [31:0] CurrentAddress_q;

  Counter #(.width(32), .max('hffffffff)) CurrentAddress (
    .count(IncAddr), .Q({CurrentAddress_q[31:18], Address, CurrentAddress_q[1:0]}), .clk(Clock), .clr(CLR));  // open: load, D, carry
  or or_1 (or_1_out, IncAddr, demultiplexer_3_out1, Finished);
  D_Flip_Flop IDLE (.clk(Clock), .D(or_1_out), .Q(IDLE_q), .preset(CLR));  // open: Qn, en, reset
  Demultiplexer #(.enable("false")) demultiplexer_1 (.out0(Load), .out1(Finished), .in(IDLE_q), .sel(End));
  D_Flip_Flop While (.clk(Clock), .D(or_2_out), .Q(While_q), .reset(CLR));  // open: Qn, preset, en
  or or_2 (or_2_out, Write, Load);
  RAM_part #(.addrWidth(18), .dataWidth(32)) ram_1 (
    .addr({Address, CurrentAddress_q[1:0]}), .data(Data), .clk(Clock));  // open: sel, ld, clr
  Demultiplexer #(.enable("false")) demultiplexer_2 (
    .out0(Write), .out1(demultiplexer_2_out1), .in(While_q), .sel(WriteEnd));
  Decoder #(.select(2)) decoder_1 (
    .out0(Mask[0]), .out1(Mask[1]), .out2(Mask[2]), .out3(Mask[3]), .sel(CurrentAddress_q[1:0]));  // open: en
  Demultiplexer #(.enable("false")) demultiplexer_3 (
    .out0(IncAddr), .out1(demultiplexer_3_out1), .in(demultiplexer_2_out1), .sel(End));
  Counter #(.width(4), .max('hf)) counter_1 (
    .load(Load), .D(WriteTime), .count(Write), .Q(counter_1_q), .clk(Clock));  // open: carry, clr
  Comparator #(.width(32)) comparator_1 (.a(Data), .b({32{1'b1}}), .eq(End));  // open: gt, lt
  Comparator #(.width(4)) comparator_2 (.a(4'b0000), .b(counter_1_q), .eq(WriteEnd));  // open: gt, lt

  // Other names for the same wires on the sheet: CLK = Clock; Count = Write; WT[3:0] = WriteTime
endmodule

module Control_Unit (
  input  [5:0] in_1,
  input  [3:0] in_2,
  input  in_3,
  input  in_4,
  input  [5:0] in_5,
  input  [3:0] in_6,
  input  in_7,
  output out_8,
  output out_9,
  output out_10,
  output out_11,
  output [3:0] out_12,
  output out_13,
  output out_14,
  output [2:0] Salidas,
  output out_16,
  output out_17,
  output out_18,
  output out_19,
  output out_20,
  output out_21,
  output [1:0] out_22,
  output [2:0] out_23,
  output [1:0] out_24,
  output out_25,
  output out_26
);

  wire ALU, and_1_out, and_4_out, Brach, CS_0, CS_1, CS_2, CS_3, CS_4, d_ff_1_q, demultiplexer_1_out1,
       demultiplexer_2_out0, demultiplexer_2_out1, demultiplexer_3_out0, demultiplexer_4_out0,
       demultiplexer_5_out0, demultiplexer_6_out0, demultiplexer_7_out1, demultiplexer_9_out0,
       demultiplexer_10_out0, Especial, Hi_Lo_Op, IDLE_q, Inmediate, LW_Inst, Next, nor_1_out, not_2_out,
       or_2_out, or_3_out, or_9_out, or_12_out, pop, R_W_3, R_W_5, R_W_6, RAM, RAM_Op1, RAM_Op2,
       Save_Instruction_q, Stack, Stack_Op1, Stack_Op2, stall, sw, SW_Inst, TTY, Wait, Wait_q;
  wire [1:0] Especial_Op;
  wire [2:0] CU_Op;
  wire [3:0] counter_1_q, RT_v_WT;

  Operation_Decoder operation_decoder_1 (
    .Entradas(in_1), .in_2(in_5), .out_3(pop), .out_4(out_10), .out_5(out_21), .out_6(out_24), .out_7(CU_Op),
    .out_8(out_12), .out_9(Salidas), .out_10(out_23), .out_11(out_20), .out_12(Especial_Op));
  Multiplexer #(.width(4), .enable("false")) multiplexer_1 (.in0(in_2), .in1(in_6), .out(RT_v_WT), .sel(out_16));
  or or_1 (out_25, CS_0, CS_1, CS_2, CS_3, CS_4);
  and and_1 (and_1_out, ALU, ~Hi_Lo_Op);  // AND_Gate
  or or_2 (or_2_out, RAM_Op1, RAM_Op2);
  or or_3 (or_3_out, Stack_Op1, Stack_Op2);
  D_Flip_Flop #(.trigger("falling")) d_ff_1 (
    .clk(in_3), .D(out_25), .Q(d_ff_1_q), .reset(in_7));  // open: Qn, preset, en
  or or_4 (out_26, and_1_out, Inmediate, R_W_3, CS_3, R_W_5, R_W_6, CS_2);
  Priority_Encoder #(.select(2), .disabled(0)) priority_encoder_1 (
    .in0(1'b1), .in1(or_2_out), .in2(or_3_out), .out(out_22), .en_in(1'b1));  // open: in3, gs, en_out
  or or_5 (out_16, SW_Inst, out_8);
  nor nor_1 (nor_1_out, counter_1_q[0], counter_1_q[1], counter_1_q[2], counter_1_q[3]);
  Counter #(.width(4), .max('hf)) counter_1 (
    .load(out_25), .D(RT_v_WT), .count(d_ff_1_q), .Q(counter_1_q), .clk(in_3));  // open: carry, clr
  not not_1 (stall, in_4);
  and and_2 (Hi_Lo_Op, out_12[3], ~out_12[2]);  // AND_Gate
  and and_3 (Wait, nor_1_out, d_ff_1_q);
  D_Flip_Flop #(.trigger("falling")) IDLE (
    .clk(in_3), .D(demultiplexer_2_out0), .Q(IDLE_q), .preset(in_7), .en(stall));  // open: Qn, reset
  Demultiplexer #(.enable("false")) demultiplexer_1 (.out0(sw), .out1(demultiplexer_1_out1), .in(RAM), .sel(out_10));
  Demultiplexer demultiplexer_2 (
    .out0(demultiplexer_2_out0), .out1(demultiplexer_2_out1), .in(IDLE_q), .sel(not_2_out));  // open: en
  not not_2 (not_2_out, in_7);
  or or_6 (RAM_Op1, demultiplexer_4_out0, sw);
  or or_7 (RAM_Op2, demultiplexer_5_out0, demultiplexer_1_out1);
  D_Flip_Flop #(.trigger("falling")) u_SW (
    .clk(in_3), .D(RAM_Op1), .Q(CS_1), .en(stall), .reset(in_7));  // open: Qn, preset
  D_Flip_Flop #(.trigger("falling")) LW (
    .clk(in_3), .D(RAM_Op2), .Q(CS_2), .en(stall), .reset(in_7));  // open: Qn, preset
  Demultiplexer #(.select(2), .enable("false")) demultiplexer_3 (
    .out0(demultiplexer_3_out0), .out1(R_W_6), .out2(R_W_5), .out3(out_17), .in(Especial), .sel(Especial_Op));
  or or_8 (CS_0, demultiplexer_6_out0, Next, demultiplexer_2_out1);
  Demultiplexer #(.enable("false")) demultiplexer_4 (
    .out0(demultiplexer_4_out0), .out1(SW_Inst), .in(CS_1), .sel(Wait));
  Demultiplexer #(.enable("false")) demultiplexer_5 (
    .out0(demultiplexer_5_out0), .out1(LW_Inst), .in(CS_2), .sel(Wait));
  or or_9 (or_9_out, out_11, demultiplexer_3_out0);
  Demultiplexer demultiplexer_6 (.out0(demultiplexer_6_out0), .out1(out_14), .in(Wait_q), .sel(Wait));  // open: en
  D_Flip_Flop #(.trigger("falling")) u_Wait (
    .clk(in_3), .D(CS_0), .Q(Wait_q), .en(stall), .reset(in_7));  // open: Qn, preset
  Demultiplexer #(.enable("false")) demultiplexer_7 (.out0(out_9), .out1(demultiplexer_7_out1), .in(Stack), .sel(pop));
  D_Flip_Flop #(.trigger("falling")) End (
    .clk(in_3), .D(or_9_out), .Q(out_11), .en(and_4_out), .reset(in_7));  // open: Qn, preset
  and and_4 (and_4_out, demultiplexer_3_out0, stall);
  D_Flip_Flop #(.trigger("falling")) Save_Instruction (
    .clk(in_3), .D(out_14), .Q(Save_Instruction_q), .en(stall), .reset(in_7));  // open: Qn, preset
  or or_10 (Stack_Op1, demultiplexer_9_out0, out_9);
  or or_11 (Stack_Op2, demultiplexer_10_out0, demultiplexer_7_out1);
  D_Flip_Flop #(.trigger("falling")) KDP (
    .clk(in_3), .D(R_W_5), .Q(out_13), .en(stall), .reset(in_7));  // open: Qn, preset
  D_Flip_Flop #(.trigger("falling")) u_TTY (
    .clk(in_3), .D(out_17), .Q(TTY), .en(stall), .reset(in_7));  // open: Qn, preset
  Demultiplexer #(.select(3)) demultiplexer_8 (
    .out0(Brach), .out1(ALU), .out2(Inmediate), .out3(R_W_3), .out4(RAM), .out5(Stack), .out6(Especial),
    .in(Save_Instruction_q), .sel(CU_Op));  // open: out7, en
  Demultiplexer demultiplexer_9 (.out0(demultiplexer_9_out0), .out1(out_8), .in(CS_4), .sel(Wait));  // open: en
  D_Flip_Flop #(.trigger("falling")) push (
    .clk(in_3), .D(Stack_Op1), .Q(CS_4), .en(stall), .reset(in_7));  // open: Qn, preset
  D_Flip_Flop #(.trigger("falling")) u_pop (
    .clk(in_3), .D(Stack_Op2), .Q(CS_3), .en(stall), .reset(in_7));  // open: Qn, preset
  Demultiplexer demultiplexer_10 (.out0(demultiplexer_10_out0), .out1(out_18), .in(CS_3), .sel(Wait));  // open: en
  D_Flip_Flop #(.trigger("falling")) u_Next (
    .clk(in_3), .D(or_12_out), .Q(Next), .en(stall), .reset(in_7));  // open: Qn, preset
  or or_12 (or_12_out, Brach, ALU, Inmediate, R_W_3, SW_Inst, LW_Inst, out_8, out_18, R_W_6, out_13, TTY);
  and and_5 (out_19, or_12_out, stall);

  // Other names for the same wires on the sheet: ALU_Op[3:0] = out_12; Branch_Op[2:0] = out_23; clk = in_3;
  //   CS = out_25; End = out_11; Func_Code[5:0] = in_5; KDP_Enable = out_13; Load_Inst = out_14; Load_PC = out_19;
  //   Logic_I = out_20; lw = out_10; Op_Code[5:0] = in_1; Pop_Inst = out_18; push = out_9; Push_Inst = out_8;
  //   R_Miss = in_4; R_W = out_26; R_W_1 = ALU; R_W_2 = Inmediate; R_W_4 = CS_3; R_W_7 = CS_2; Read_Time[3:0] = in_2;
  //   Register = R_W_3; Reset = in_7; rt_rd = out_21; RW_RAM = out_16; Select_Adress[1:0] = out_22;
  //   Select_B[1:0] = out_24; Select_DI[2:0] = Salidas; TTY_Enable = out_17; Write_Time[3:0] = in_6

  // Notes on the sheet:
  //   Entradas
  //   Auxiliars
  //   Type Intruction Selector
  //   Next Intruction
endmodule

module Operation_Decoder (
  input  [5:0] Entradas,
  input  [5:0] in_2,
  output out_3,
  output out_4,
  output out_5,
  output [1:0] out_6,
  output [2:0] out_7,
  output [3:0] out_8,
  output [2:0] out_9,
  output [2:0] out_10,
  output out_11,
  output [1:0] out_12
);

  wire add, addi, ALU, \and , and_6_out, and_7_out, and_8_out, and_9_out, and_10_out, and_11_out, and_22_out,
       and_23_out, and_24_out, and_25_out, and_26_out, and_27_out, and_36_out, and_37_out, and_38_out,
       and_39_out, and_40_out, and_51_out, and_52_out, and_53_out, and_54_out, and_55_out, andi, beq, bgtz,
       blez, bltz, bne, Brach, Cond_Jump, div, divu, Especial, Func_000000, halt, Inmediate, j, jr, kbd,
       mfhi, mflo, mult, Mult_Div, mulu, nop, \nor , Op_000000, Op_111000, Op_111111, \or , or_1_out,
       or_2_out, or_6_out, or_7_out, or_10_out, or_11_out, or_12_out, or_13_out, or_14_out, or_17_out,
       or_19_out, ori, priority_encoder_2_gs, push, RAM, Register, rnd, slt, slti, sltiu, sltu, Stack, sub,
       sw, tty, \xor , xori;

  and and_1 (Op_000000, ~Entradas[0], ~Entradas[1], ~Entradas[2], ~Entradas[3], ~Entradas[4], ~Entradas[5]);  // AND_Gate
  and and_2 (Func_000000, ~in_2[0], ~in_2[1], ~in_2[2], ~in_2[3], ~in_2[4], ~in_2[5]);  // AND_Gate
  and and_3 (Op_111000, ~Entradas[0], ~Entradas[1], ~Entradas[2], Entradas[3], Entradas[4], Entradas[5]);  // AND_Gate
  and and_4 (Op_111111, Entradas[0], Entradas[1], Entradas[2], Entradas[3], Entradas[4], Entradas[5]);
  and and_5 (j, ~Entradas[0], Entradas[1], ~Entradas[2], ~Entradas[3], ~Entradas[4], ~Entradas[5]);  // AND_Gate
  or or_1 (or_1_out, 1'b1, halt);
  and and_6 (and_6_out, ~in_2[0], ~in_2[1], ~in_2[2], ~in_2[3], ~in_2[4], in_2[5]);  // AND_Gate
  and and_7 (and_7_out, ~in_2[0], in_2[1], ~in_2[2], ~in_2[3], ~in_2[4], in_2[5]);  // AND_Gate
  and and_8 (and_8_out, ~in_2[0], ~in_2[1], ~in_2[2], in_2[3], in_2[4], ~in_2[5]);  // AND_Gate
  and and_9 (and_9_out, in_2[0], ~in_2[1], ~in_2[2], in_2[3], in_2[4], ~in_2[5]);  // AND_Gate
  and and_10 (and_10_out, ~in_2[0], in_2[1], ~in_2[2], in_2[3], in_2[4], ~in_2[5]);  // AND_Gate
  and and_11 (and_11_out, in_2[0], in_2[1], ~in_2[2], in_2[3], in_2[4], ~in_2[5]);  // AND_Gate
  and and_12 (addi, ~Entradas[0], ~Entradas[1], ~Entradas[2], Entradas[3], ~Entradas[4], ~Entradas[5]);  // AND_Gate
  and and_13 (andi, ~Entradas[0], ~Entradas[1], Entradas[2], Entradas[3], ~Entradas[4], ~Entradas[5]);  // AND_Gate
  Priority_Encoder #(.select(2), .disabled(0)) priority_encoder_1 (
    .in0(or_1_out), .in1(rnd), .in2(kbd), .in3(tty), .out(out_12), .en_in(1'b1));  // open: gs, en_out
  Priority_Encoder #(.disabled(0)) priority_encoder_2 (
    .in0(1'b1), .in1(beq), .in2(bne), .in3(blez), .in4(bgtz), .in5(bltz), .in6(j), .in7(jr), .out(out_10),
    .en_in(1'b1), .gs(priority_encoder_2_gs));  // open: en_out
  and and_14 (add, Op_000000, and_6_out);
  and and_15 (sub, Op_000000, and_7_out);
  and and_16 (mult, Op_000000, and_8_out);
  and and_17 (mulu, Op_000000, and_9_out);
  and and_18 (div, Op_000000, and_10_out);
  and and_19 (divu, Op_000000, and_11_out);
  or or_2 (or_2_out, out_3, out_4);
  or or_3 (ALU, add, mulu, mult, \or , slt, \nor , div, \xor , sltu, \and , divu, sub);
  Priority_Encoder #(.disabled(0)) priority_encoder_3 (
    .in0(1'b1), .in1(or_2_out), .in2(mfhi), .in3(mflo), .in4(kbd), .in5(rnd), .out(out_9), .en_in(1'b1));  // open: in6, in7, gs, en_out
  and and_20 (ori, Entradas[0], ~Entradas[1], Entradas[2], Entradas[3], ~Entradas[4], ~Entradas[5]);  // AND_Gate
  and and_21 (xori, ~Entradas[0], Entradas[1], Entradas[2], Entradas[3], ~Entradas[4], ~Entradas[5]);  // AND_Gate
  and and_22 (and_22_out, ~in_2[0], ~in_2[1], in_2[2], ~in_2[3], ~in_2[4], in_2[5]);  // AND_Gate
  and and_23 (and_23_out, in_2[0], ~in_2[1], in_2[2], ~in_2[3], ~in_2[4], in_2[5]);  // AND_Gate
  and and_24 (and_24_out, in_2[0], in_2[1], in_2[2], ~in_2[3], ~in_2[4], in_2[5]);  // AND_Gate
  and and_25 (and_25_out, ~in_2[0], ~in_2[1], ~in_2[2], in_2[3], ~in_2[4], in_2[5]);  // AND_Gate
  and and_26 (and_26_out, ~in_2[0], in_2[1], ~in_2[2], in_2[3], ~in_2[4], in_2[5]);  // AND_Gate
  and and_27 (and_27_out, in_2[0], in_2[1], ~in_2[2], in_2[3], ~in_2[4], in_2[5]);  // AND_Gate
  Priority_Encoder #(.disabled(0)) priority_encoder_4 (
    .in0(Brach), .in1(ALU), .in2(Inmediate), .in3(Register), .in4(RAM), .in5(Stack), .in6(Especial),
    .out(out_7), .en_in(1'b1));  // open: in7, gs, en_out
  or or_4 (out_5, Op_111000, Op_000000, Op_111111);
  and and_28 (\and , Op_000000, and_22_out);
  and and_29 (\or , Op_000000, and_23_out);
  and and_30 (\nor , Op_000000, and_24_out);
  and and_31 (\xor , Op_000000, and_25_out);
  and and_32 (slt, Op_000000, and_26_out);
  and and_33 (sltu, Op_000000, and_27_out);
  and and_34 (slti, ~Entradas[0], Entradas[1], ~Entradas[2], Entradas[3], ~Entradas[4], ~Entradas[5]);  // AND_Gate
  and and_35 (sltiu, Entradas[0], Entradas[1], ~Entradas[2], Entradas[3], ~Entradas[4], ~Entradas[5]);  // AND_Gate
  or or_5 (Brach, bne, bgtz, blez, j, jr, nop, beq, bltz);
  or or_6 (or_6_out, bgtz, blez, bltz);
  or or_7 (or_7_out, Inmediate, RAM);
  Priority_Encoder #(.select(2), .disabled(0)) priority_encoder_5 (
    .in0(1'b1), .in1(or_6_out), .in2(or_7_out), .out(out_6), .en_in(1'b1));  // open: in3, gs, en_out
  and and_36 (and_36_out, ~in_2[0], ~in_2[1], ~in_2[2], ~in_2[3], in_2[4], ~in_2[5]);  // AND_Gate
  and and_37 (and_37_out, ~in_2[0], in_2[1], ~in_2[2], ~in_2[3], in_2[4], ~in_2[5]);  // AND_Gate
  and and_38 (and_38_out, ~in_2[0], ~in_2[1], ~in_2[2], in_2[3], ~in_2[4], ~in_2[5]);  // AND_Gate
  and and_39 (and_39_out, ~in_2[0], ~in_2[1], ~in_2[2], ~in_2[3], ~in_2[4], ~in_2[5]);  // AND_Gate
  and and_40 (and_40_out, in_2[0], ~in_2[1], ~in_2[2], ~in_2[3], ~in_2[4], ~in_2[5]);  // AND_Gate
  and and_41 (bne, Entradas[0], ~Entradas[1], Entradas[2], ~Entradas[3], ~Entradas[4], ~Entradas[5]);  // AND_Gate
  and and_42 (blez, ~Entradas[0], Entradas[1], Entradas[2], ~Entradas[3], ~Entradas[4], ~Entradas[5]);  // AND_Gate
  and and_43 (bgtz, Entradas[0], Entradas[1], Entradas[2], ~Entradas[3], ~Entradas[4], ~Entradas[5]);  // AND_Gate
  or or_8 (Cond_Jump, bne, bgtz, beq, blez, bltz);
  and and_44 (mfhi, Op_000000, and_36_out);
  and and_45 (mflo, Op_000000, and_37_out);
  and and_46 (jr, Op_000000, and_38_out);
  and and_47 (out_3, Op_111000, and_39_out);
  and and_48 (push, Op_111000, and_40_out);
  and and_49 (beq, ~Entradas[0], ~Entradas[1], Entradas[2], ~Entradas[3], ~Entradas[4], ~Entradas[5]);  // AND_Gate
  and and_50 (bltz, Entradas[0], ~Entradas[1], ~Entradas[2], ~Entradas[3], ~Entradas[4], ~Entradas[5]);  // AND_Gate
  or or_9 (Inmediate, addi, xori, ori, slti, sltiu, andi);
  or or_10 (or_10_out, RAM, addi, add);
  or or_11 (or_11_out, Cond_Jump, sub);
  or or_12 (or_12_out, \and , andi);
  or or_13 (or_13_out, \or , ori);
  or or_14 (or_14_out, \xor , xori);
  or or_15 (out_11, ori, xori, andi);
  or or_16 (Register, mflo, mfhi);
  or or_17 (or_17_out, slt, slti);
  or or_18 (Stack, out_3, push);
  or or_19 (or_19_out, sltiu, sltu);
  and and_51 (and_51_out, ~ALU, ~Inmediate, ~RAM, ~Cond_Jump);  // AND_Gate
  and and_52 (and_52_out, in_2[0], in_2[1], in_2[2], in_2[3], in_2[4], in_2[5]);
  and and_53 (and_53_out, in_2[0], ~in_2[1], ~in_2[2], ~in_2[3], ~in_2[4], ~in_2[5]);  // AND_Gate
  and and_54 (and_54_out, ~in_2[0], in_2[1], ~in_2[2], ~in_2[3], ~in_2[4], ~in_2[5]);  // AND_Gate
  and and_55 (and_55_out, ~in_2[0], ~in_2[1], in_2[2], ~in_2[3], ~in_2[4], ~in_2[5]);  // AND_Gate
  and and_56 (nop, Op_000000, Func_000000);
  or or_20 (Especial, kbd, rnd, tty, halt);
  or or_21 (RAM, out_4, sw);
  Priority_Encoder #(.select(4), .disabled(0)) priority_encoder_6 (
    .in0(or_10_out), .in1(or_11_out), .in2(or_12_out), .in3(or_13_out), .in4(\nor ), .in5(or_14_out),
    .in6(or_17_out), .in7(or_19_out), .in8(mult), .in9(div), .in10(mulu), .in11(divu), .in15(and_51_out),
    .out(out_8), .en_in(1'b1));  // open: in12, in13, in14, gs, en_out
  and and_57 (halt, Op_111111, and_52_out);
  and and_58 (tty, Op_111111, and_53_out);
  and and_59 (rnd, Op_111111, and_54_out);
  and and_60 (kbd, Op_111111, and_55_out);
  and and_61 (out_4, Entradas[0], Entradas[1], ~Entradas[2], ~Entradas[3], ~Entradas[4], Entradas[5]);  // AND_Gate
  and and_62 (sw, Entradas[0], Entradas[1], ~Entradas[2], Entradas[3], ~Entradas[4], Entradas[5]);  // AND_Gate
  or or_22 (Mult_Div, mult, divu, div, mulu);

  // Other names for the same wires on the sheet: ALU_Op[3:0] = out_8; Branch_Op[2:0] = out_10; CU_Op[2:0] = out_7;
  //   Especial_Op[1:0] = out_12; Func_code[5:0] = in_2; Logical_Inmediate = out_11; lw = out_4;
  //   Op_code[5:0] = Entradas; pop = out_3; rt_rd = out_5; Select_B[1:0] = out_6; Select_DI[2:0] = out_9

  // Notes on the sheet:
  //   Op_Types
  //   Tipo I
  //   Clasificaciones
  //   Salidas
  //   ALU_Ops
  //   ALU
  //   Register_Ops
  //   Stack_Ops
  //   Branch
  //   Especial_Ops
  //   RAM
endmodule

module Data_Path (
  input  in_1,
  input  in_2,
  input  [2:0] in_3,
  input  in_4,
  input  [1:0] in_5,
  input  [3:0] in_6,
  input  [1:0] in_7,
  input  [2:0] in_8,
  input  in_9,
  input  in_10,
  input  [31:0] in_11,
  input  in_12,
  input  [6:0] in_13,
  input  in_14,
  input  in_15,
  input  in_16,
  input  in_17,
  input  in_18,
  output [5:0] out_19,
  output [31:0] out_20,
  output [31:0] out_21,
  output [5:0] out_22,
  output [6:0] out_23
);

  wire Hi_Lo_Enable, NF, or_1_out, ZF;
  wire [4:0] Rd, Rs, Rt, SDA;
  wire [5:0] Op_Code;
  wire [15:0] Const;
  wire [25:0] Jump_Rute, Rute;
  wire [31:0] ALU, bit_extender_1_out, DA, DATA, Hi, High, Inst, KBD, KBD_t, Lo, Low, Offset, PC, PC_prime,
       Rand_Generator, RT__prime, RT_t, Sp;
  wire [31:7] RS_t;

  Program_Counter program_counter_1 (.in_1(PC_prime), .in_2(in_18), .in_3(in_15), .in_4(in_10), .out_5(PC));
  Branch_Control branch_control_1 (
    .in_1(PC), .in_2(Rute), .in_3(Offset), .in_4(in_8), .in_5({RS_t, out_23}), .out_8(PC_prime), .in_6(ZF),
    .in_7(NF));
  assign bit_extender_1_out = {{25{1'b0}}, in_13};  // Bit_Extender bit_extender_1
  Random #(.width(32)) random_1 (.clk(in_18), .next(in_18), .out(Rand_Generator));  // open: clr
  Multiplexer #(.width(32), .enable("false")) multiplexer_1 (
    .in0({32{1'b1}}), .in1(bit_extender_1_out), .out(KBD), .sel(in_14));
  Intruction_Decoder intruction_decoder_1 (
    .out_2(Op_Code), .out_3(Rs), .out_4(Rt), .out_5(Jump_Rute), .out_6(Rd), .out_7(Const), .out_8(out_22),
    .in_1(Inst));
  Register #(.width(32)) register_1 (.D(in_11), .en(in_12), .Q(Inst), .clk(in_18), .clr(in_15));
  Register #(.width(32)) register_2 (.D(in_11), .en(in_18), .Q(DATA), .clk(in_18), .clr(in_15));
  Register_File register_file_1 (
    .in_1(DA), .in_2(Rs), .in_3(Rt), .in_4(SDA), .in_5(in_18), .in_7(in_1), .in_9(in_15),
    .out_10({RS_t, out_23}), .out_11(RT_t), .out_12(Sp), .in_6(in_17), .in_8(in_16));
  Multiplexer #(.width(5), .enable("false")) multiplexer_2 (.in0(Rt), .in1(Rd), .out(SDA), .sel(in_2));
  Multiplexer #(.select(3), .width(32), .enable("false")) multiplexer_3 (
    .in0(ALU), .in1(DATA), .in2(High), .in3(Low), .in4(KBD_t), .in5(Rand_Generator), .out(DA), .sel(in_3));  // open: in6, in7
  Sign_Extender sign_extender_1 (.in_1(Const), .in_2(in_4), .out_3(Offset));
  Multiplexer #(.select(2), .width(32), .enable("false")) multiplexer_4 (
    .in0(RT_t), .in1({32{1'b0}}), .in2(Offset), .out(RT__prime), .sel(in_7));  // open: in3
  ALU alu_1 (
    .in_1({RS_t, out_23}), .in_2(RT__prime), .in_3(in_6), .out_4(ALU), .out_5(Hi), .out_6(Lo), .out_7(ZF),
    .out_8(NF));
  and and_1 (Hi_Lo_Enable, in_6[3], ~in_6[2]);  // AND_Gate
  Register #(.width(32)) register_3 (.D(Hi), .en(Hi_Lo_Enable), .Q(High), .clk(in_18), .clr(in_15));
  Register #(.width(32)) register_4 (.D(Lo), .en(Hi_Lo_Enable), .Q(Low), .clk(in_18), .clr(in_15));
  Multiplexer #(.width(32), .enable("false")) multiplexer_5 (
    .in0(RT_t), .in1({RS_t, out_23}), .out(out_21), .sel(or_1_out));
  or or_1 (or_1_out, in_17, in_9);
  Multiplexer #(.select(2), .width(32)) multiplexer_6 (
    .in0(PC), .in1(ALU), .in2(Sp), .out(out_20), .sel(in_5));  // open: in3, en

  // Other names for the same wires on the sheet: Adress[31:0] = out_20; Adress_Select[1:0] = in_5;
  //   ALU_Select[3:0] = in_6; ALU_Select_B[1:0] = in_7; BS[2:0] = in_8; clk = in_18; DA_Select = in_2;
  //   Data_Select[2:0] = in_3; Enable_Inst = in_12; Enable_PC = in_10; Func_Code[5:0] = out_22; KBD_Avalible = in_14;
  //   KBD_Data[6:0] = in_13; Op_Code_t[5:0] = out_19; pop = in_16; push = in_17; push_end = in_9; R_W = in_1;
  //   RAM_DATA[31:0] = in_11; Reset = in_15; RS_t[6:0] = out_23; TTY_DATA[6:0] = out_23; SE_Select = in_4;
  //   Value[31:0] = out_21

  // Notes on the sheet:
  //   Entradas
  //   DATA PATH
  //   COMPONENTES
  //   COMPLEMENTOS
  //   Salidas
endmodule

module Program_Counter (
  input  [31:0] in_1,
  input  in_2,
  input  in_3,
  input  in_4,
  output [31:0] out_5
);

  Register #(.width(32)) register_1 (.D(in_1), .en(in_4), .Q(out_5), .clk(in_2), .clr(in_3));

  // Other names for the same wires on the sheet: clk = in_2; Data[31:0] = in_1; Enable = in_4; Reset = in_3

  // Notes on the sheet:
  //   PC
endmodule

module Branch_Control (
  input  [31:0] in_1,
  input  [25:0] in_2,
  input  [31:0] in_3,
  input  [2:0] in_4,
  input  [31:0] in_5,
  input  in_6,
  input  in_7,
  output [31:0] out_8
);

  wire and_1_out, and_2_out, and_3_out, and_4_out, and_5_out, beq, bgtz, blez, bltz, bne, brach_Jump, j, jr,
       nop, Rs____0;
  wire [1:0] S_Jump;
  wire [31:0] multiplier_1_out, PC___4, PC___4___4___Offset;

  Decoder #(.select(3), .enable("false")) decoder_1 (
    .out0(nop), .out1(beq), .out2(bne), .out3(blez), .out4(bgtz), .out5(bltz), .out6(j), .out7(jr), .sel(in_4));
  and and_1 (and_1_out, beq, in_6);
  and and_2 (and_2_out, bne, ~in_6);  // AND_Gate
  and and_3 (and_3_out, blez, Rs____0);
  and and_4 (and_4_out, bgtz, ~Rs____0);  // AND_Gate
  and and_5 (and_5_out, bltz, in_7);
  Adder #(.width(32)) adder_1 (.a(in_1), .b(32'h4), .out(PC___4));  // open: cin, cout
  Multiplier #(.width(32)) multiplier_1 (.a(in_3), .b(32'h4), .out(multiplier_1_out));  // open: cin, cout
  Adder #(.width(32)) adder_2 (.a(PC___4), .b(multiplier_1_out), .out(PC___4___4___Offset));  // open: cin, cout
  or or_1 (Rs____0, in_6, in_7);
  or or_2 (brach_Jump, and_1_out, and_2_out, and_3_out, and_4_out, and_5_out);
  Priority_Encoder #(.select(2)) priority_encoder_1 (
    .in0(1'b1), .in1(brach_Jump), .in2(j), .in3(jr), .out(S_Jump), .en_in(1'b1));  // open: gs, en_out
  Multiplexer #(.select(2), .width(32), .enable("false")) multiplexer_1 (
    .in0(PC___4), .in1(PC___4___4___Offset), .in2({2'b00, in_2, in_1[3:0]}), .in3(in_5), .out(out_8),
    .sel(S_Jump));

  // Other names for the same wires on the sheet: B_Selector[2:0] = in_4; Jump[29:0] = {in_2, in_1[3:0]};
  //   PC[31:0] = in_1; Rute[25:0] = in_2; NF = in_7; Offset[31:0] = in_3; PC_prime[31:0] = out_8; RS[31:0] = in_5;
  //   ZF = in_6

  // Notes on the sheet:
  //   Branch Control
endmodule

module Intruction_Decoder (
  input  [31:0] in_1,
  output [5:0] out_2,
  output [4:0] out_3,
  output [4:0] out_4,
  output [25:0] out_5,
  output [4:0] out_6,
  output [15:0] out_7,
  output [5:0] out_8
);


  assign out_2 = in_1[31:26];
  assign out_3 = in_1[25:21];
  assign out_4 = in_1[20:16];
  assign out_5 = in_1[25:0];
  assign out_6 = in_1[15:11];
  assign out_7 = in_1[15:0];
  assign out_8 = in_1[5:0];

  // Other names for the same wires on the sheet: Constant[15:0] = in_1[15:0]; Func_Code[5:0] = in_1[5:0];
  //   Intruction[31:0] = in_1; Jump_Rute[25:0] = in_1[25:0]; Rd[4:0] = in_1[15:11]; Rt[4:0] = in_1[20:16];
  //   Rs[4:0] = in_1[25:21]; Op_Code[5:0] = in_1[31:26]

  // Notes on the sheet:
  //   Intruction Decoder
endmodule

module Register_File (
  input  [31:0] in_1,
  input  [4:0] in_2,
  input  [4:0] in_3,
  input  [4:0] in_4,
  input  in_5,
  input  in_6,
  input  in_7,
  input  in_8,
  input  in_9,
  output [31:0] out_10,
  output [31:0] out_11,
  output [31:0] out_12
);

  wire adder_1_cout, demultiplexer_1_out0, Enable_1, Enable_2, Enable_3, Enable_4, Enable_5, Enable_6,
       Enable_7, Enable_8, Enable_9, Enable_10, Enable_11, Enable_12, Enable_13, Enable_14, Enable_15,
       Enable_16, Enable_17, Enable_18, Enable_19, Enable_20, Enable_21, Enable_22, Enable_23, Enable_24,
       Enable_25, Enable_26, Enable_27, Enable_28, Enable_29, Enable_30, Enable_31, or_1_out;
  wire [1:0] priority_encoder_1_out;
  wire [31:0] adder_1_out, multiplexer_4_out, R0, R1, R2, R3, R4, R5, R6, R7, R8, R9, R10, R11, R12, R13,
       R14, R15, R16, R17, R18, R19, R20, R21, R22, R23, R24, R25, R26, R27, R28, R29, R30, R31,
       subtractor_1_out;

  Multiplexer #(.select(5), .width(32)) multiplexer_1 (
    .in0(R0), .in1(R1), .in2(R2), .in3(R3), .in4(R4), .in5(R5), .in6(R6), .in7(R7), .in8(R8), .in9(R9),
    .in10(R10), .in11(R11), .in12(R12), .in13(R13), .in14(R14), .in15(R15), .in16(R16), .in18(R18),
    .in19(R19), .in20(R20), .in21(R21), .in22(R22), .in23(R23), .in24(R24), .in25(R25), .in26(R26),
    .in27(R27), .in28(R28), .in29(R29), .in30(R30), .in31(R31), .out(out_10), .sel(in_2));  // open: in17, en
  Demultiplexer #(.select(5)) demultiplexer_1 (
    .out0(demultiplexer_1_out0), .out1(Enable_1), .out2(Enable_2), .out3(Enable_3), .out4(Enable_4),
    .out5(Enable_5), .out6(Enable_6), .out7(Enable_7), .out8(Enable_8), .out9(Enable_9), .out10(Enable_10),
    .out11(Enable_11), .out12(Enable_12), .out13(Enable_13), .out14(Enable_14), .out15(Enable_15),
    .out16(Enable_16), .out17(Enable_17), .out18(Enable_18), .out19(Enable_19), .out20(Enable_20),
    .out21(Enable_21), .out22(Enable_22), .out23(Enable_23), .out24(Enable_24), .out25(Enable_25),
    .out26(Enable_26), .out27(Enable_27), .out28(Enable_28), .out29(Enable_29), .out30(Enable_30),
    .out31(Enable_31), .in(in_7), .sel(in_4));  // open: en
  Multiplexer #(.select(5), .width(32)) multiplexer_2 (
    .in0(R0), .in1(R1), .in2(R2), .in3(R3), .in4(R4), .in5(R5), .in6(R6), .in7(R7), .in8(R8), .in9(R9),
    .in10(R10), .in11(R11), .in12(R12), .in13(R13), .in14(R14), .in15(R15), .in16(R16), .in18(R18),
    .in19(R19), .in20(R20), .in21(R21), .in22(R22), .in23(R23), .in24(R24), .in25(R25), .in26(R26),
    .in27(R27), .in28(R28), .in29(R29), .in30(R30), .in31(R31), .out(out_11), .sel(in_3));  // open: in17, en
  Register #(.width(32)) register_1 (.D({32{1'b0}}), .Q(R0), .clk(in_5), .clr(in_9));  // open: en
  Register #(.width(32)) register_2 (.D(in_1), .en(Enable_1), .Q(R1), .clk(in_5), .clr(in_9));
  Register #(.width(32)) register_3 (.D(in_1), .en(Enable_2), .Q(R2), .clk(in_5), .clr(in_9));
  Register #(.width(32)) register_4 (.D(in_1), .en(Enable_3), .Q(R3), .clk(in_5), .clr(in_9));
  Register #(.width(32)) register_5 (.D(in_1), .en(Enable_4), .Q(R4), .clk(in_5), .clr(in_9));
  Register #(.width(32)) register_6 (.D(in_1), .en(Enable_5), .Q(R5), .clk(in_5), .clr(in_9));
  Register #(.width(32)) register_7 (.D(in_1), .en(Enable_6), .Q(R6), .clk(in_5), .clr(in_9));
  Register #(.width(32)) register_8 (.D(in_1), .en(Enable_7), .Q(R7), .clk(in_5), .clr(in_9));
  Register #(.width(32)) register_9 (.D(in_1), .en(Enable_8), .Q(R8), .clk(in_5), .clr(in_9));
  Register #(.width(32)) register_10 (.D(in_1), .en(Enable_9), .Q(R9), .clk(in_5), .clr(in_9));
  Register #(.width(32)) register_11 (.D(in_1), .en(Enable_10), .Q(R10), .clk(in_5), .clr(in_9));
  Register #(.width(32)) register_12 (.D(in_1), .en(Enable_11), .Q(R11), .clk(in_5), .clr(in_9));
  Register #(.width(32)) register_13 (.D(in_1), .en(Enable_12), .Q(R12), .clk(in_5), .clr(in_9));
  Register #(.width(32)) register_14 (.D(in_1), .en(Enable_13), .Q(R13), .clk(in_5), .clr(in_9));
  Register #(.width(32)) register_15 (.D(in_1), .en(Enable_14), .Q(R14), .clk(in_5), .clr(in_9));
  Register #(.width(32)) register_16 (.D(in_1), .en(Enable_15), .Q(R15), .clk(in_5), .clr(in_9));
  Register #(.width(32)) register_17 (.D(in_1), .en(Enable_16), .Q(R16), .clk(in_5), .clr(in_9));
  Register #(.width(32)) register_18 (.D(in_1), .en(Enable_17), .Q(R17), .clk(in_5), .clr(in_9));
  Register #(.width(32)) register_19 (.D(in_1), .en(Enable_18), .Q(R18), .clk(in_5), .clr(in_9));
  Register #(.width(32)) register_20 (.D(in_1), .en(Enable_19), .Q(R19), .clk(in_5), .clr(in_9));
  Register #(.width(32)) register_21 (.D(in_1), .en(Enable_20), .Q(R20), .clk(in_5), .clr(in_9));
  Register #(.width(32)) register_22 (.D(in_1), .en(Enable_21), .Q(R21), .clk(in_5), .clr(in_9));
  Register #(.width(32)) register_23 (.D(in_1), .en(Enable_22), .Q(R22), .clk(in_5), .clr(in_9));
  Register #(.width(32)) register_24 (.D(in_1), .en(Enable_23), .Q(R23), .clk(in_5), .clr(in_9));
  Register #(.width(32)) register_25 (.D(in_1), .en(Enable_24), .Q(R24), .clk(in_5), .clr(in_9));
  Register #(.width(32)) register_26 (.D(in_1), .en(Enable_25), .Q(R25), .clk(in_5), .clr(in_9));
  Register #(.width(32)) register_27 (.D(in_1), .en(Enable_26), .Q(R26), .clk(in_5), .clr(in_9));
  Register #(.width(32)) register_28 (.D(in_1), .en(Enable_27), .Q(R27), .clk(in_5), .clr(in_9));
  Register #(.width(32)) register_29 (.D(in_1), .en(Enable_28), .Q(R28), .clk(in_5), .clr(in_9));
  Register #(.width(32)) register_30 (.D(in_1), .en(Enable_29), .Q(R29), .clk(in_5), .clr(in_9));
  Register #(.width(32)) register_31 (.D(in_1), .en(Enable_30), .Q(R30), .clk(in_5), .clr(in_9));
  Adder #(.width(32)) adder_1 (.a(R31), .b(32'h4), .out(adder_1_out), .cout(adder_1_cout));  // open: cin
  Subtractor #(.width(32)) subtractor_1 (.a(R31), .b(32'h4), .out(subtractor_1_out), .bin(adder_1_cout));  // open: bout
  Priority_Encoder #(.select(2)) priority_encoder_1 (
    .in0(1'b1), .in1(in_6), .in2(in_8), .in3(in_9), .out(priority_encoder_1_out));
  Multiplexer #(.width(32), .enable("false")) multiplexer_3 (
    .in0(R31), .in1(subtractor_1_out), .out(out_12), .sel(in_8));
  Multiplexer #(.select(2), .width(32)) multiplexer_4 (
    .in0(in_1), .in1(adder_1_out), .in2(subtractor_1_out), .in3(32'h3ffff), .out(multiplexer_4_out),
    .sel(priority_encoder_1_out));  // open: en
  or or_1 (or_1_out, in_6, in_8, Enable_31, in_9);
  Register #(.width(32)) register_32 (.D(multiplexer_4_out), .en(or_1_out), .Q(R31), .clk(in_5));  // open: clr

  // Other names for the same wires on the sheet: A[31:0] = out_10; B[31:0] = out_11; clk = in_5; Data[31:0] = in_1;
  //   pop = in_6; push = in_8; R_W = in_7; Reset = in_9; Selector_A[4:0] = in_2; Selector_B[4:0] = in_3;
  //   Selector_Data[4:0] = in_4; SP[31:0] = out_12

  // Notes on the sheet:
  //   Entradas
  //   A Selector
  //   B Selector
  //   Data Selector
  //   Registros
  //   Salidas
endmodule

module ALU (
  input  [31:0] in_1,
  input  [31:0] in_2,
  input  [3:0] in_3,
  output [31:0] out_4,
  output [31:0] out_5,
  output [31:0] out_6,
  output out_7,
  output out_8
);

  wire comparator_1_lt, comparator_2_lt;
  wire [31:0] add, \and , Div, Divr, Divu, Divur, Mult, Multr, Mulu, Mulur, \nor , \or , slt, sltu, sub,
       \xor ;

  Mult_Signed mult_signed_1 (.in_1(in_1), .in_2(in_2), .out_3(Mult), .out_4(Multr));
  Multiplier #(.width(32)) multiplier_1 (.a(in_1), .b(in_2), .out(Mulu), .cout(Mulur));  // open: cin
  Divider #(.width(32)) divider_1 (.a(in_1), .b(in_2), .out(Divu), .rem(Divur));  // open: upper
  Div_Signed div_signed_1 (.in_1(in_1), .out_3(Div), .in_2(in_2), .out_4(Divr));
  Adder #(.width(32)) adder_1 (.a(in_1), .b(in_2), .out(add));  // open: cin, cout
  Subtractor #(.width(32)) subtractor_1 (.a(in_1), .b(in_2), .out(sub));  // open: bin, bout
  assign \and  = in_1 & in_2;  // AND_Gate and_1, 32 bits wide
  assign \or  = in_1 | in_2;  // OR_Gate or_1, 32 bits wide
  assign \nor  = ~(in_1 | in_2);  // NOR_Gate nor_1, 32 bits wide
  assign \xor  = in_1 ^ in_2;  // XOR_Gate xor_1, 32 bits wide
  Comparator #(.width(32)) comparator_1 (.a(in_1), .b(in_2), .lt(comparator_1_lt));  // open: gt, eq
  Comparator #(.width(32), .mode("unsigned")) comparator_2 (.a(in_1), .b(in_2), .lt(comparator_2_lt));  // open: gt, eq
  assign slt = {{31{1'b0}}, comparator_1_lt};  // Bit_Extender bit_extender_1
  assign sltu = {{31{1'b0}}, comparator_2_lt};  // Bit_Extender bit_extender_2
  Comparator #(.width(32)) comparator_3 (.a({32{1'b0}}), .b(out_4), .eq(out_7));  // open: gt, lt
  Multiplexer #(.select(2), .width(32)) multiplexer_1 (
    .in0(Multr), .in1(Divr), .in2(Mulur), .in3(Divur), .out(out_5), .sel(in_3[1:0]));  // open: en
  Multiplexer #(.select(2), .width(32)) multiplexer_2 (
    .in0(Mult), .in1(Div), .in2(Mulu), .in3(Divu), .out(out_6), .sel(in_3[1:0]));  // open: en
  Multiplexer #(.select(3), .width(32)) multiplexer_3 (
    .in0(add), .in1(sub), .in2(\and ), .in3(\or ), .in4(\nor ), .in5(\xor ), .in6(slt), .in7(sltu),
    .out(out_4), .sel(in_3[2:0]));  // open: en

  assign out_8 = out_4[0];

  // Other names for the same wires on the sheet: Hi[31:0] = out_5; Lo[31:0] = out_6; NF = out_4[0]; Rd[31:0] = out_4;
  //   Rs[31:0] = in_1; Rt[31:0] = in_2; Selector[2:0] = in_3[2:0]; Selector_ALU[3:0] = in_3;
  //   Selector_Hi_Lo[1:0] = in_3[1:0]; ZF = out_7

  // Notes on the sheet:
  //   Entradas
  //   ALU
  //   Salidas
endmodule

module Mult_Signed (
  input  [31:0] in_1,
  input  [31:0] in_2,
  output [31:0] out_3,
  output [31:0] out_4
);

  wire A_2_31, adder_3_cout, adder_4_cout, B_2_31, comparator_1_eq, comparator_2_eq, Especial, Especial_A,
       Especial_B;
  wire [30:0] Carry_Especial;
  wire [31:0] _00_Carry, _00_Rd, _01_Carry, _01_Rd, _10_Carry, _10_Rd, _11_Carry, _11_Rd, bit_extender_1_out,
       bit_extender_2_out, Carry_Normal, multiplier_3_cout, multiplier_3_out, multiplier_4_cout,
       multiplier_4_out, nA, nand_1_out, nand_2_out, nand_3_out, nand_4_out, nB, Rd_Normal;
  wire [31:31] Mult_Especial;

  Negator #(.width(32)) negator_1 (.in(in_1), .out(nA));
  Negator #(.width(32)) negator_2 (.in(in_2), .out(nB));
  Multiplier #(.width(32)) multiplier_1 (.a(in_1), .b(in_2), .out(_00_Rd), .cout(_00_Carry));  // open: cin
  Comparator #(.width(31)) comparator_1 (.a(in_1[30:0]), .b({31{1'b0}}), .eq(comparator_1_eq));  // open: gt, lt
  Comparator #(.width(31)) comparator_2 (.a(in_2[30:0]), .b({31{1'b0}}), .eq(comparator_2_eq));  // open: gt, lt
  Multiplier #(.width(32)) multiplier_2 (.a(nA), .b(nB), .out(_11_Rd), .cout(_11_Carry));  // open: cin
  and and_1 (A_2_31, in_1[31], comparator_1_eq);
  and and_2 (B_2_31, in_2[31], comparator_2_eq);
  Multiplier #(.width(32)) multiplier_3 (
    .a(in_1), .b(nB), .out(multiplier_3_out), .cout(multiplier_3_cout));  // open: cin
  Multiplier #(.width(32)) multiplier_4 (
    .a(nA), .b(in_2), .out(multiplier_4_out), .cout(multiplier_4_cout));  // open: cin
  and and_3 (Especial_A, in_2[31], A_2_31);
  and and_4 (Especial_B, B_2_31, in_1[31]);
  assign nand_1_out = ~(multiplier_3_out & {32{1'b1}});  // NAND_Gate nand_1, 32 bits wide
  assign nand_2_out = ~(multiplier_3_cout & {32{1'b1}});  // NAND_Gate nand_2, 32 bits wide
  assign bit_extender_1_out = {{31{1'b0}}, adder_3_cout};  // Bit_Extender bit_extender_1
  assign nand_3_out = ~(multiplier_4_out & {32{1'b1}});  // NAND_Gate nand_3, 32 bits wide
  assign nand_4_out = ~(multiplier_4_cout & {32{1'b1}});  // NAND_Gate nand_4, 32 bits wide
  assign bit_extender_2_out = {{31{1'b0}}, adder_4_cout};  // Bit_Extender bit_extender_2
  Adder #(.width(32)) adder_1 (.a(nand_2_out), .b(bit_extender_1_out), .out(_01_Carry));  // open: cin, cout
  Adder #(.width(32)) adder_2 (.a(nand_4_out), .b(bit_extender_2_out), .out(_10_Carry));  // open: cin, cout
  or or_1 (Especial, Especial_A, Especial_B);
  Adder #(.width(32)) adder_3 (.a(nand_1_out), .b(32'h1), .out(_01_Rd), .cout(adder_3_cout));  // open: cin
  Adder #(.width(32)) adder_4 (.a(nand_3_out), .b(32'h1), .out(_10_Rd), .cout(adder_4_cout));  // open: cin
  Multiplexer #(.width(32)) multiplexer_1 (
    .in0(nA), .in1(nB), .out({Carry_Especial, Mult_Especial[31]}), .sel(Especial_A));  // open: en
  Multiplexer #(.select(2), .width(32), .enable("false")) multiplexer_2 (
    .in0(_00_Rd), .in1(_01_Rd), .in2(_10_Rd), .in3(_11_Rd), .out(Rd_Normal), .sel({in_1[31], in_2[31]}));
  Multiplexer #(.select(2), .width(32), .enable("false")) multiplexer_3 (
    .in0(_00_Carry), .in1(_01_Carry), .in2(_10_Carry), .in3(_11_Carry), .out(Carry_Normal),
    .sel({in_1[31], in_2[31]}));
  Multiplexer #(.width(32)) multiplexer_4 (
    .in0(Rd_Normal), .in1({Mult_Especial[31], {31{1'b0}}}), .out(out_3), .sel(Especial));  // open: en
  Multiplexer #(.width(32)) multiplexer_5 (
    .in0(Carry_Normal), .in1({1'b0, Carry_Especial}), .out(out_4), .sel(Especial));  // open: en

  // Other names for the same wires on the sheet: B[31:0] = in_2; B_Sign = in_2[31]; A[31:0] = in_1; A_Sign = in_1[31];
  //   A_31[30:0] = in_1[30:0]; B_31[30:0] = in_2[30:0]; Carry[31:0] = out_4;
  //   nChose[31:0] = {Carry_Especial, Mult_Especial[31]}; Rd[31:0] = out_3

  // Notes on the sheet:
  //   Entradas
  //   Especial
  //   Mult Signo
  //   Salidas
endmodule

module Div_Signed (
  input  [31:0] in_1,
  input  [31:0] in_2,
  output [31:0] out_3,
  output [31:0] out_4
);

  wire [31:0] _00, _00_C, _01, _01_C, _10, _10_C, _11, _11_C, divider_1_rem, divider_3_out, divider_4_out,
       divider_4_rem, negator_1_out, negator_2_out, negator_4_out, negator_5_out;

  Negator #(.width(32)) negator_1 (.in(in_1), .out(negator_1_out));
  Negator #(.width(32)) negator_2 (.in(in_2), .out(negator_2_out));
  Divider #(.width(32)) divider_1 (
    .a(negator_1_out), .b(negator_2_out), .out(_11), .rem(divider_1_rem));  // open: upper
  Negator #(.width(32)) negator_3 (.in(divider_1_rem), .out(_11_C));
  Divider #(.width(32)) divider_2 (.a(in_1), .b(in_2), .out(_00), .rem(_00_C));  // open: upper
  Negator #(.width(32)) negator_4 (.in(in_1), .out(negator_4_out));
  Divider #(.width(32)) divider_3 (.a(in_1), .b(negator_5_out), .out(divider_3_out), .rem(_01_C));  // open: upper
  Negator #(.width(32)) negator_5 (.in(in_2), .out(negator_5_out));
  Divider #(.width(32)) divider_4 (
    .a(negator_4_out), .b(in_2), .out(divider_4_out), .rem(divider_4_rem));  // open: upper
  Negator #(.width(32)) negator_6 (.in(divider_4_rem), .out(_10_C));
  Negator #(.width(32)) negator_7 (.in(divider_3_out), .out(_01));
  Negator #(.width(32)) negator_8 (.in(divider_4_out), .out(_10));
  Multiplexer #(.select(2), .width(32), .enable("false")) multiplexer_1 (
    .in0(_00), .in1(_01), .in2(_10), .in3(_11), .out(out_3), .sel({in_1[31], in_2[31]}));
  Multiplexer #(.select(2), .width(32), .enable("false")) multiplexer_2 (
    .in0(_00_C), .in1(_01_C), .in2(_10_C), .in3(_11_C), .out(out_4), .sel({in_1[31], in_2[31]}));

  // Other names for the same wires on the sheet: B[31:0] = in_2; A[31:0] = in_1; BMS_B = in_2[31]; BMS_A = in_1[31];
  //   Carry[31:0] = out_4; Rd[31:0] = out_3

  // Notes on the sheet:
  //   Entradas
  //   Div Signo
  //   Salidas
endmodule

module Sign_Extender (
  input  [15:0] in_1,
  input  in_2,
  output [31:0] out_3
);

  wire [31:0] bit_extender_1_out, bit_extender_2_out;

  assign bit_extender_1_out = {{16{in_1[15]}}, in_1};  // Bit_Extender bit_extender_1
  assign bit_extender_2_out = {{16{1'b0}}, in_1};  // Bit_Extender bit_extender_2
  Multiplexer #(.width(32)) multiplexer_1 (
    .in0(bit_extender_1_out), .in1(bit_extender_2_out), .out(out_3), .sel(in_2));  // open: en

  // Other names for the same wires on the sheet: Input[15:0] = in_1; Output[31:0] = out_3; Sign = in_2

  // Notes on the sheet:
  //   Sign Extender
endmodule

module RAM_Manager (
  input  [31:0] in_1,
  input  [31:0] in_2,
  input  [31:0] in_3,
  input  in_4,
  input  [31:0] in_5,
  input  [31:0] in_6,
  input  [31:0] in_7,
  input  in_8,
  input  in_9,
  output [15:0] out_10,
  output [3:0] out_11,
  output [31:0] out_12,
  output [1:0] out_13
);

  wire [15:2] divider_1_rem;
  wire [31:0] multiplexer_1_out, shifter_1_out;

  Shifter #(.width(32), .shift("lr")) shifter_1 (.in(in_3), .\dist (5'b00010), .out(shifter_1_out));
  Divider #(.width(16)) divider_1 (
    .a(shifter_1_out[15:0]), .b(16'h4), .out(out_10), .rem({divider_1_rem, out_13}));  // open: upper
  Decoder #(.select(2), .enable("false")) decoder_1 (
    .out0(out_11[0]), .out1(out_11[1]), .out2(out_11[2]), .out3(out_11[3]), .sel(out_13));
  Multiplexer #(.select(2), .width(32), .enable("false")) multiplexer_1 (
    .in0(in_1), .in1(in_2), .in2(in_5), .in3(in_6), .out(multiplexer_1_out), .sel(out_13));
  Multiplexer #(.width(32), .enable("false")) multiplexer_2 (
    .in0(multiplexer_1_out), .in1(in_7), .out({out_12[7:0], out_12[15:8], out_12[23:16], out_12[31:24]}),
    .sel(in_4));

  // Other names for the same wires on the sheet: Bank[1:0] = out_13; Adress_In[31:0] = in_3;
  //   Adress_Out[15:0] = out_10; Cache_out[31:0] = in_7; clk = in_8; Hit = in_4; Mask[3:0] = out_11;
  //   RAM_Out[31:0] = out_12; RAM_OUTPUT_0[31:0] = in_1; RAM_OUTPUT_1[31:0] = in_2; RAM_OUTPUT_2[31:0] = in_5;
  //   RAM_OUTPUT_3[31:0] = in_6; Reset = in_9

  // Notes on the sheet:
  //   Entradas
  //   Salidas
  //   Little Endian - Big Endian
endmodule

module Cache (
  input  in_1,
  input  in_2,
  input  in_3,
  input  in_4,
  input  [1:0] in_5,
  input  [31:0] in_6,
  input  [15:0] in_7,
  output out_8,
  output out_9,
  output [31:0] out_10
);

  wire and_3_out, and_4_out, and_5_out, and_6_out, and_7_out, comparator_1_eq, Hit, or_1_out, or_2_out,
       or_3_out, or_8_out, read_0, read_00, read_01, read_1, read_10, read_11, read_20, read_21, read_30,
       read_31, s_00, s_01, s_10, s_11, s_20, s_21, s_30, s_31, store_0, store_00, store_01, store_1,
       store_2, store_3, store_10, store_11, store_20, store_21, store_30, store_31, Valid, Valid_0, Valid_1,
       write_0, write_1;
  wire [10:0] tag_Out, tag_Out_0, tag_Out_1;
  wire [31:0] RAM_Out_0, RAM_Out_00, RAM_Out_01, RAM_Out_1, RAM_Out_10, RAM_Out_11, RAM_Out_20, RAM_Out_21,
       RAM_Out_30, RAM_Out_31;

  Demultiplexer #(.select(2), .enable("false")) demultiplexer_1 (
    .out0(store_0), .out1(store_1), .out2(store_2), .out3(store_3), .in(in_2), .sel(in_5));
  Comparator #(.width(11)) comparator_1 (.a({in_7[15:6], 1'b1}), .b(tag_Out), .eq(comparator_1_eq));  // open: gt, lt
  and and_1 (out_8, in_4, ~Hit);  // AND_Gate
  Demultiplexer #(.enable("false")) demultiplexer_2 (.out0(read_0), .out1(read_1), .in(out_8), .sel(in_7[5]));
  and and_2 (Hit, comparator_1_eq, Valid);
  Demultiplexer #(.enable("false")) demultiplexer_3 (.out0(store_00), .out1(store_01), .in(store_0), .sel(in_7[5]));
  Demultiplexer #(.enable("false")) demultiplexer_4 (.out0(store_10), .out1(store_11), .in(store_1), .sel(in_7[5]));
  and and_3 (and_3_out, Hit, in_4);
  Demultiplexer #(.enable("false")) demultiplexer_5 (.out0(write_0), .out1(write_1), .in(and_3_out), .sel(in_7[5]));
  Demultiplexer #(.enable("false")) demultiplexer_6 (.out0(store_20), .out1(store_21), .in(store_2), .sel(in_7[5]));
  Demultiplexer #(.enable("false")) demultiplexer_7 (.out0(store_30), .out1(store_31), .in(store_3), .sel(in_7[5]));
  Tag_Data tag_data_1 (
    .in_1({in_7[15:6], 1'b1}), .in_2(in_7[4:0]), .in_3(in_1), .in_4(in_3), .in_5(or_1_out), .out_6(tag_Out_0));
  and and_4 (and_4_out, in_2, ~in_7[5]);  // AND_Gate
  Valid_Data valid_data_1 (.in_1(in_7[4:0]), .in_2(in_1), .in_3(in_3), .in_4(or_2_out), .out_5(Valid_0));
  or or_1 (or_1_out, and_4_out, read_0);
  or or_2 (or_2_out, and_5_out, read_0);
  and and_5 (and_5_out, in_2, ~in_7[5]);  // AND_Gate
  Demultiplexer #(.select(2), .enable("false")) demultiplexer_8 (
    .out0(read_00), .out1(read_10), .out2(read_20), .out3(read_30), .in(write_0), .sel(in_5));
  Demultiplexer #(.select(2), .enable("false")) demultiplexer_9 (
    .out0(read_01), .out1(read_11), .out2(read_21), .out3(read_31), .in(write_1), .sel(in_5));
  Tag_Data tag_data_2 (
    .in_1({in_7[15:6], 1'b1}), .in_2(in_7[4:0]), .in_3(in_1), .in_4(in_3), .in_5(or_8_out), .out_6(tag_Out_1));
  Multiplexer #(.width(11), .enable("false")) multiplexer_1 (
    .in0(tag_Out_0), .in1(tag_Out_1), .out(tag_Out), .sel(in_7[5]));
  Valid_Data valid_data_2 (.in_1(in_7[4:0]), .in_2(in_1), .in_3(in_3), .in_4(or_3_out), .out_5(Valid_1));
  Multiplexer #(.enable("false")) multiplexer_2 (.in0(Valid_0), .in1(Valid_1), .out(Valid), .sel(in_7[5]));
  or or_3 (or_3_out, and_6_out, read_1);
  and and_6 (and_6_out, in_2, in_7[5]);
  or or_4 (s_00, store_00, read_00);
  or or_5 (s_10, store_10, read_10);
  or or_6 (s_20, store_20, read_20);
  or or_7 (s_30, store_30, read_30);
  or or_8 (or_8_out, and_7_out, read_1);
  and and_7 (and_7_out, in_2, in_7[5]);
  or or_9 (s_01, store_01, read_01);
  or or_10 (s_11, store_11, read_11);
  or or_11 (s_21, store_21, read_21);
  or or_12 (s_31, store_31, read_31);
  Bank_Data bank_data_1 (.in_1(in_6), .in_2(in_7[4:0]), .in_3(in_1), .in_4(in_3), .in_5(s_00), .out_6(RAM_Out_00));
  Bank_Data bank_data_2 (.in_1(in_6), .in_2(in_7[4:0]), .in_3(in_1), .in_4(in_3), .in_5(s_10), .out_6(RAM_Out_10));
  Bank_Data bank_data_3 (.in_1(in_6), .in_2(in_7[4:0]), .in_3(in_1), .in_4(in_3), .in_5(s_20), .out_6(RAM_Out_20));
  Bank_Data bank_data_4 (.in_1(in_6), .in_2(in_7[4:0]), .in_3(in_1), .in_4(in_3), .in_5(s_30), .out_6(RAM_Out_30));
  Bank_Data bank_data_5 (.in_1(in_6), .in_2(in_7[4:0]), .in_3(in_1), .in_4(in_3), .in_5(s_01), .out_6(RAM_Out_01));
  Bank_Data bank_data_6 (.in_1(in_6), .in_2(in_7[4:0]), .in_3(in_1), .in_4(in_3), .in_5(s_11), .out_6(RAM_Out_11));
  Bank_Data bank_data_7 (.in_1(in_6), .in_2(in_7[4:0]), .in_3(in_1), .in_4(in_3), .in_5(s_21), .out_6(RAM_Out_21));
  Bank_Data bank_data_8 (.in_1(in_6), .in_2(in_7[4:0]), .in_3(in_1), .in_4(in_3), .in_5(s_31), .out_6(RAM_Out_31));
  and and_8 (out_9, Hit, in_4);
  Multiplexer #(.select(2), .width(32), .enable("false")) multiplexer_3 (
    .in0(RAM_Out_00), .in1(RAM_Out_10), .in2(RAM_Out_20), .in3(RAM_Out_30), .out(RAM_Out_0), .sel(in_5));
  Multiplexer #(.select(2), .width(32), .enable("false")) multiplexer_4 (
    .in0(RAM_Out_01), .in1(RAM_Out_11), .in2(RAM_Out_21), .in3(RAM_Out_31), .out(RAM_Out_1), .sel(in_5));
  Multiplexer #(.width(32), .enable("false")) multiplexer_5 (
    .in0(RAM_Out_0), .in1(RAM_Out_1), .out(out_10), .sel(in_7[5]));

  // Other names for the same wires on the sheet: adr[4:0] = in_7[4:0]; adress[15:0] = in_7; offset = in_7[5];
  //   Bank[1:0] = in_5; clk = in_1; Pop_lw = in_4; R_Miss = out_8; RAM_Out[31:0] = out_10; Reset = in_3; store = in_2;
  //   tag_In[10:1] = in_7[15:6]; Value[31:0] = in_6

  // Notes on the sheet:
  //   Entradas
  //   Tag_Data
  //   Valid_Data
  //   Banks
  //   Salidas
endmodule

module Tag_Data (
  input  [10:0] in_1,
  input  [4:0] in_2,
  input  in_3,
  input  in_4,
  input  in_5,
  output [10:0] out_6
);

  wire Enable_0, Enable_1, Enable_2, Enable_3, Enable_4, Enable_5, Enable_6, Enable_7, Enable_8, Enable_9,
       Enable_10, Enable_11, Enable_12, Enable_13, Enable_14, Enable_15, Enable_16, Enable_17, Enable_18,
       Enable_19, Enable_20, Enable_21, Enable_22, Enable_23, Enable_24, Enable_25, Enable_26, Enable_27,
       Enable_28, Enable_29, Enable_30, Enable_31;
  wire [10:0] tag_0, tag_1, tag_2, tag_3, tag_4, tag_5, tag_6, tag_7, tag_8, tag_9, tag_10, tag_11, tag_12,
       tag_13, tag_14, tag_15, tag_16, tag_17, tag_18, tag_19, tag_20, tag_21, tag_22, tag_23, tag_24,
       tag_25, tag_26, tag_27, tag_28, tag_29, tag_30, tag_31;

  Demultiplexer #(.select(5), .enable("false")) demultiplexer_1 (
    .out0(Enable_0), .out1(Enable_1), .out2(Enable_2), .out3(Enable_3), .out4(Enable_4), .out5(Enable_5),
    .out6(Enable_6), .out7(Enable_7), .out8(Enable_8), .out9(Enable_9), .out10(Enable_10), .out11(Enable_11),
    .out12(Enable_12), .out13(Enable_13), .out14(Enable_14), .out15(Enable_15), .out16(Enable_16),
    .out17(Enable_17), .out18(Enable_18), .out19(Enable_19), .out20(Enable_20), .out21(Enable_21),
    .out22(Enable_22), .out23(Enable_23), .out24(Enable_24), .out25(Enable_25), .out26(Enable_26),
    .out27(Enable_27), .out28(Enable_28), .out29(Enable_29), .out30(Enable_30), .out31(Enable_31), .in(in_5),
    .sel(in_2));
  Register #(.width(11)) register_1 (.D(in_1), .en(Enable_0), .Q(tag_0), .clk(in_3), .clr(in_4));
  Register #(.width(11)) register_2 (.D(in_1), .en(Enable_4), .Q(tag_4), .clk(in_3), .clr(in_4));
  Register #(.width(11)) register_3 (.D(in_1), .en(Enable_8), .Q(tag_8), .clk(in_3), .clr(in_4));
  Register #(.width(11)) register_4 (.D(in_1), .en(Enable_12), .Q(tag_12), .clk(in_3), .clr(in_4));
  Register #(.width(11)) register_5 (.D(in_1), .en(Enable_16), .Q(tag_16), .clk(in_3), .clr(in_4));
  Register #(.width(11)) register_6 (.D(in_1), .en(Enable_20), .Q(tag_20), .clk(in_3), .clr(in_4));
  Register #(.width(11)) register_7 (.D(in_1), .en(Enable_24), .Q(tag_24), .clk(in_3), .clr(in_4));
  Register #(.width(11)) register_8 (.D(in_1), .en(Enable_28), .Q(tag_28), .clk(in_3), .clr(in_4));
  Register #(.width(11)) register_9 (.D(in_1), .en(Enable_1), .Q(tag_1), .clk(in_3), .clr(in_4));
  Register #(.width(11)) register_10 (.D(in_1), .en(Enable_5), .Q(tag_5), .clk(in_3), .clr(in_4));
  Register #(.width(11)) register_11 (.D(in_1), .en(Enable_9), .Q(tag_9), .clk(in_3), .clr(in_4));
  Register #(.width(11)) register_12 (.D(in_1), .en(Enable_13), .Q(tag_13), .clk(in_3), .clr(in_4));
  Register #(.width(11)) register_13 (.D(in_1), .en(Enable_17), .Q(tag_17), .clk(in_3), .clr(in_4));
  Register #(.width(11)) register_14 (.D(in_1), .en(Enable_21), .Q(tag_21), .clk(in_3), .clr(in_4));
  Register #(.width(11)) register_15 (.D(in_1), .en(Enable_25), .Q(tag_25), .clk(in_3), .clr(in_4));
  Register #(.width(11)) register_16 (.D(in_1), .en(Enable_29), .Q(tag_29), .clk(in_3), .clr(in_4));
  Register #(.width(11)) register_17 (.D(in_1), .en(Enable_2), .Q(tag_2), .clk(in_3), .clr(in_4));
  Register #(.width(11)) register_18 (.D(in_1), .en(Enable_6), .Q(tag_6), .clk(in_3), .clr(in_4));
  Register #(.width(11)) register_19 (.D(in_1), .en(Enable_10), .Q(tag_10), .clk(in_3), .clr(in_4));
  Register #(.width(11)) register_20 (.D(in_1), .en(Enable_14), .Q(tag_14), .clk(in_3), .clr(in_4));
  Register #(.width(11)) register_21 (.D(in_1), .en(Enable_18), .Q(tag_18), .clk(in_3), .clr(in_4));
  Register #(.width(11)) register_22 (.D(in_1), .en(Enable_22), .Q(tag_22), .clk(in_3), .clr(in_4));
  Register #(.width(11)) register_23 (.D(in_1), .en(Enable_26), .Q(tag_26), .clk(in_3), .clr(in_4));
  Register #(.width(11)) register_24 (.D(in_1), .en(Enable_30), .Q(tag_30), .clk(in_3), .clr(in_4));
  Register #(.width(11)) register_25 (.D(in_1), .en(Enable_3), .Q(tag_3), .clk(in_3), .clr(in_4));
  Register #(.width(11)) register_26 (.D(in_1), .en(Enable_7), .Q(tag_7), .clk(in_3), .clr(in_4));
  Register #(.width(11)) register_27 (.D(in_1), .en(Enable_11), .Q(tag_11), .clk(in_3), .clr(in_4));
  Register #(.width(11)) register_28 (.D(in_1), .en(Enable_15), .Q(tag_15), .clk(in_3), .clr(in_4));
  Register #(.width(11)) register_29 (.D(in_1), .en(Enable_19), .Q(tag_19), .clk(in_3), .clr(in_4));
  Register #(.width(11)) register_30 (.D(in_1), .en(Enable_23), .Q(tag_23), .clk(in_3), .clr(in_4));
  Register #(.width(11)) register_31 (.D(in_1), .en(Enable_27), .Q(tag_27), .clk(in_3), .clr(in_4));
  Register #(.width(11)) register_32 (.D(in_1), .en(Enable_31), .Q(tag_31), .clk(in_3), .clr(in_4));
  Multiplexer #(.select(5), .width(11), .enable("false")) multiplexer_1 (
    .in0(tag_0), .in1(tag_1), .in2(tag_2), .in3(tag_3), .in4(tag_4), .in5(tag_5), .in6(tag_6), .in7(tag_7),
    .in8(tag_8), .in9(tag_9), .in10(tag_10), .in11(tag_11), .in12(tag_12), .in13(tag_13), .in14(tag_14),
    .in15(tag_15), .in16(tag_16), .in17(tag_17), .in18(tag_18), .in19(tag_19), .in20(tag_20), .in21(tag_21),
    .in22(tag_22), .in23(tag_23), .in24(tag_24), .in25(tag_25), .in26(tag_26), .in27(tag_27), .in28(tag_28),
    .in29(tag_29), .in30(tag_30), .in31(tag_31), .out(out_6), .sel(in_2));

  // Other names for the same wires on the sheet: adr[4:0] = in_2; clk = in_3; R_W = in_5; Reset = in_4;
  //   tag_In[10:0] = in_1; tag_Out[10:0] = out_6

  // Notes on the sheet:
  //   Entradas
  //   Registros
  //   Salidas
endmodule

module Valid_Data (
  input  [4:0] in_1,
  input  in_2,
  input  in_3,
  input  in_4,
  output out_5
);

  wire Enable_0, Enable_1, Enable_2, Enable_3, Enable_4, Enable_5, Enable_6, Enable_7, Enable_8, Enable_9,
       Enable_10, Enable_11, Enable_12, Enable_13, Enable_14, Enable_15, Enable_16, Enable_17, Enable_18,
       Enable_19, Enable_20, Enable_21, Enable_22, Enable_23, Enable_24, Enable_25, Enable_26, Enable_27,
       Enable_28, Enable_29, Enable_30, Enable_31, Valid_0, Valid_4, Valid_8, Valid_10, Valid_12, Valid_20,
       Valid_28, Valid__1, Valid__2, Valid__3, Valid__5, Valid__6, Valid__7, Valid__9, Valid__11, Valid__13,
       Valid__14, Valid__15, Valid__16, Valid__17, Valid__18, Valid__19, Valid__21, Valid__22, Valid__23,
       Valid__24, Valid__25, Valid__26, Valid__27, Valid__29, Valid__30, Valid__31;

  Demultiplexer #(.select(5), .enable("false")) demultiplexer_1 (
    .out0(Enable_0), .out1(Enable_1), .out2(Enable_2), .out3(Enable_3), .out4(Enable_4), .out5(Enable_5),
    .out6(Enable_6), .out7(Enable_7), .out8(Enable_8), .out9(Enable_9), .out10(Enable_10), .out11(Enable_11),
    .out12(Enable_12), .out13(Enable_13), .out14(Enable_14), .out15(Enable_15), .out16(Enable_16),
    .out17(Enable_17), .out18(Enable_18), .out19(Enable_19), .out20(Enable_20), .out21(Enable_21),
    .out22(Enable_22), .out23(Enable_23), .out24(Enable_24), .out25(Enable_25), .out26(Enable_26),
    .out27(Enable_27), .out28(Enable_28), .out29(Enable_29), .out30(Enable_30), .out31(Enable_31), .in(in_4),
    .sel(in_1));
  Register #(.width(1)) register_1 (.D(in_4), .en(Enable_0), .Q(Valid_0), .clk(in_2), .clr(in_3));
  Register #(.width(1)) register_2 (.D(in_4), .en(Enable_4), .Q(Valid_4), .clk(in_2), .clr(in_3));
  Register #(.width(1)) register_3 (.D(in_4), .en(Enable_8), .Q(Valid_8), .clk(in_2), .clr(in_3));
  Register #(.width(1)) register_4 (.D(in_4), .en(Enable_12), .Q(Valid_12), .clk(in_2), .clr(in_3));
  Register #(.width(1)) register_5 (.D(in_4), .en(Enable_16), .Q(Valid__16), .clk(in_2), .clr(in_3));
  Register #(.width(1)) register_6 (.D(in_4), .en(Enable_20), .Q(Valid_20), .clk(in_2), .clr(in_3));
  Register #(.width(1)) register_7 (.D(in_4), .en(Enable_24), .Q(Valid__24), .clk(in_2), .clr(in_3));
  Register #(.width(1)) register_8 (.D(in_4), .en(Enable_28), .Q(Valid_28), .clk(in_2), .clr(in_3));
  Register #(.width(1)) register_9 (.D(in_4), .en(Enable_1), .Q(Valid__1), .clk(in_2), .clr(in_3));
  Register #(.width(1)) register_10 (.D(in_4), .en(Enable_5), .Q(Valid__5), .clk(in_2), .clr(in_3));
  Register #(.width(1)) register_11 (.D(in_4), .en(Enable_9), .Q(Valid__9), .clk(in_2), .clr(in_3));
  Register #(.width(1)) register_12 (.D(in_4), .en(Enable_13), .Q(Valid__13), .clk(in_2), .clr(in_3));
  Register #(.width(1)) register_13 (.D(in_4), .en(Enable_17), .Q(Valid__17), .clk(in_2), .clr(in_3));
  Register #(.width(1)) register_14 (.D(in_4), .en(Enable_21), .Q(Valid__21), .clk(in_2), .clr(in_3));
  Register #(.width(1)) register_15 (.D(in_4), .en(Enable_25), .Q(Valid__25), .clk(in_2), .clr(in_3));
  Register #(.width(1)) register_16 (.D(in_4), .en(Enable_29), .Q(Valid__29), .clk(in_2), .clr(in_3));
  Register #(.width(1)) register_17 (.D(in_4), .en(Enable_2), .Q(Valid__2), .clk(in_2), .clr(in_3));
  Register #(.width(1)) register_18 (.D(in_4), .en(Enable_6), .Q(Valid__6), .clk(in_2), .clr(in_3));
  Register #(.width(1)) register_19 (.D(in_4), .en(Enable_10), .Q(Valid_10), .clk(in_2), .clr(in_3));
  Register #(.width(1)) register_20 (.D(in_4), .en(Enable_14), .Q(Valid__14), .clk(in_2), .clr(in_3));
  Register #(.width(1)) register_21 (.D(in_4), .en(Enable_18), .Q(Valid__18), .clk(in_2), .clr(in_3));
  Register #(.width(1)) register_22 (.D(in_4), .en(Enable_22), .Q(Valid__22), .clk(in_2), .clr(in_3));
  Register #(.width(1)) register_23 (.D(in_4), .en(Enable_26), .Q(Valid__26), .clk(in_2), .clr(in_3));
  Register #(.width(1)) register_24 (.D(in_4), .en(Enable_30), .Q(Valid__30), .clk(in_2), .clr(in_3));
  Register #(.width(1)) register_25 (.D(in_4), .en(Enable_3), .Q(Valid__3), .clk(in_2), .clr(in_3));
  Register #(.width(1)) register_26 (.D(in_4), .en(Enable_7), .Q(Valid__7), .clk(in_2), .clr(in_3));
  Register #(.width(1)) register_27 (.D(in_4), .en(Enable_11), .Q(Valid__11), .clk(in_2), .clr(in_3));
  Register #(.width(1)) register_28 (.D(in_4), .en(Enable_15), .Q(Valid__15), .clk(in_2), .clr(in_3));
  Register #(.width(1)) register_29 (.D(in_4), .en(Enable_19), .Q(Valid__19), .clk(in_2), .clr(in_3));
  Register #(.width(1)) register_30 (.D(in_4), .en(Enable_23), .Q(Valid__23), .clk(in_2), .clr(in_3));
  Register #(.width(1)) register_31 (.D(in_4), .en(Enable_27), .Q(Valid__27), .clk(in_2), .clr(in_3));
  Register #(.width(1)) register_32 (.D(in_4), .en(Enable_31), .Q(Valid__31), .clk(in_2), .clr(in_3));
  Multiplexer #(.select(5), .enable("false")) multiplexer_1 (
    .in0(Valid_0), .in1(Valid__1), .in2(Valid__2), .in3(Valid__3), .in4(Valid_4), .in5(Valid__5),
    .in6(Valid__6), .in7(Valid__7), .in8(Valid_8), .in9(Valid__9), .in10(Valid_10), .in11(Valid__11),
    .in12(Valid_12), .in13(Valid__13), .in14(Valid__14), .in15(Valid__15), .in16(Valid__16),
    .in17(Valid__17), .in18(Valid__18), .in19(Valid__19), .in20(Valid_20), .in21(Valid__21),
    .in22(Valid__22), .in23(Valid__23), .in24(Valid__24), .in25(Valid__25), .in26(Valid__26),
    .in27(Valid__27), .in28(Valid_28), .in29(Valid__29), .in30(Valid__30), .in31(Valid__31), .out(out_5),
    .sel(in_1));

  // Other names for the same wires on the sheet: adr[4:0] = in_1; clk = in_2; R_W = in_4; Reset = in_3

  // Notes on the sheet:
  //   Entradas
  //   Registros
  //   Salidas
endmodule

module Bank_Data (
  input  [31:0] in_1,
  input  [4:0] in_2,
  input  in_3,
  input  in_4,
  input  in_5,
  output [31:0] out_6
);

  wire Enable_0, Enable_1, Enable_2, Enable_3, Enable_4, Enable_5, Enable_6, Enable_7, Enable_8, Enable_9,
       Enable_10, Enable_11, Enable_12, Enable_13, Enable_14, Enable_15, Enable_16, Enable_17, Enable_18,
       Enable_19, Enable_20, Enable_21, Enable_22, Enable_23, Enable_24, Enable_25, Enable_26, Enable_27,
       Enable_28, Enable_29, Enable_30, Enable_31;
  wire [31:0] RAM_0, RAM_1, RAM_2, RAM_3, RAM_4, RAM_5, RAM_6, RAM_7, RAM_8, RAM_9, RAM_10, RAM_11, RAM_12,
       RAM_13, RAM_14, RAM_15, RAM_16, RAM_17, RAM_18, RAM_19, RAM_20, RAM_21, RAM_22, RAM_23, RAM_24,
       RAM_25, RAM_26, RAM_27, RAM_28, RAM_29, RAM_30, RAM_31;

  Demultiplexer #(.select(5), .enable("false")) demultiplexer_1 (
    .out0(Enable_0), .out1(Enable_1), .out2(Enable_2), .out3(Enable_3), .out4(Enable_4), .out5(Enable_5),
    .out6(Enable_6), .out7(Enable_7), .out8(Enable_8), .out9(Enable_9), .out10(Enable_10), .out11(Enable_11),
    .out12(Enable_12), .out13(Enable_13), .out14(Enable_14), .out15(Enable_15), .out16(Enable_16),
    .out17(Enable_17), .out18(Enable_18), .out19(Enable_19), .out20(Enable_20), .out21(Enable_21),
    .out22(Enable_22), .out23(Enable_23), .out24(Enable_24), .out25(Enable_25), .out26(Enable_26),
    .out27(Enable_27), .out28(Enable_28), .out29(Enable_29), .out30(Enable_30), .out31(Enable_31), .in(in_5),
    .sel(in_2));
  Register #(.width(32)) register_1 (.D(in_1), .en(Enable_0), .Q(RAM_0), .clk(in_3), .clr(in_4));
  Register #(.width(32)) register_2 (.D(in_1), .en(Enable_4), .Q(RAM_4), .clk(in_3), .clr(in_4));
  Register #(.width(32)) register_3 (.D(in_1), .en(Enable_8), .Q(RAM_8), .clk(in_3), .clr(in_4));
  Register #(.width(32)) register_4 (.D(in_1), .en(Enable_12), .Q(RAM_12), .clk(in_3), .clr(in_4));
  Register #(.width(32)) register_5 (.D(in_1), .en(Enable_16), .Q(RAM_16), .clk(in_3), .clr(in_4));
  Register #(.width(32)) register_6 (.D(in_1), .en(Enable_20), .Q(RAM_20), .clk(in_3), .clr(in_4));
  Register #(.width(32)) register_7 (.D(in_1), .en(Enable_24), .Q(RAM_24), .clk(in_3), .clr(in_4));
  Register #(.width(32)) register_8 (.D(in_1), .en(Enable_28), .Q(RAM_28), .clk(in_3), .clr(in_4));
  Register #(.width(32)) register_9 (.D(in_1), .en(Enable_1), .Q(RAM_1), .clk(in_3), .clr(in_4));
  Register #(.width(32)) register_10 (.D(in_1), .en(Enable_5), .Q(RAM_5), .clk(in_3), .clr(in_4));
  Register #(.width(32)) register_11 (.D(in_1), .en(Enable_9), .Q(RAM_9), .clk(in_3), .clr(in_4));
  Register #(.width(32)) register_12 (.D(in_1), .en(Enable_13), .Q(RAM_13), .clk(in_3), .clr(in_4));
  Register #(.width(32)) register_13 (.D(in_1), .en(Enable_17), .Q(RAM_17), .clk(in_3), .clr(in_4));
  Register #(.width(32)) register_14 (.D(in_1), .en(Enable_21), .Q(RAM_21), .clk(in_3), .clr(in_4));
  Register #(.width(32)) register_15 (.D(in_1), .en(Enable_25), .Q(RAM_25), .clk(in_3), .clr(in_4));
  Register #(.width(32)) register_16 (.D(in_1), .en(Enable_29), .Q(RAM_29), .clk(in_3), .clr(in_4));
  Register #(.width(32)) register_17 (.D(in_1), .en(Enable_2), .Q(RAM_2), .clk(in_3), .clr(in_4));
  Register #(.width(32)) register_18 (.D(in_1), .en(Enable_6), .Q(RAM_6), .clk(in_3), .clr(in_4));
  Register #(.width(32)) register_19 (.D(in_1), .en(Enable_10), .Q(RAM_10), .clk(in_3), .clr(in_4));
  Register #(.width(32)) register_20 (.D(in_1), .en(Enable_14), .Q(RAM_14), .clk(in_3), .clr(in_4));
  Register #(.width(32)) register_21 (.D(in_1), .en(Enable_18), .Q(RAM_18), .clk(in_3), .clr(in_4));
  Register #(.width(32)) register_22 (.D(in_1), .en(Enable_22), .Q(RAM_22), .clk(in_3), .clr(in_4));
  Register #(.width(32)) register_23 (.D(in_1), .en(Enable_26), .Q(RAM_26), .clk(in_3), .clr(in_4));
  Register #(.width(32)) register_24 (.D(in_1), .en(Enable_30), .Q(RAM_30), .clk(in_3), .clr(in_4));
  Register #(.width(32)) register_25 (.D(in_1), .en(Enable_3), .Q(RAM_3), .clk(in_3), .clr(in_4));
  Register #(.width(32)) register_26 (.D(in_1), .en(Enable_7), .Q(RAM_7), .clk(in_3), .clr(in_4));
  Register #(.width(32)) register_27 (.D(in_1), .en(Enable_11), .Q(RAM_11), .clk(in_3), .clr(in_4));
  Register #(.width(32)) register_28 (.D(in_1), .en(Enable_15), .Q(RAM_15), .clk(in_3), .clr(in_4));
  Register #(.width(32)) register_29 (.D(in_1), .en(Enable_19), .Q(RAM_19), .clk(in_3), .clr(in_4));
  Register #(.width(32)) register_30 (.D(in_1), .en(Enable_23), .Q(RAM_23), .clk(in_3), .clr(in_4));
  Register #(.width(32)) register_31 (.D(in_1), .en(Enable_27), .Q(RAM_27), .clk(in_3), .clr(in_4));
  Register #(.width(32)) register_32 (.D(in_1), .en(Enable_31), .Q(RAM_31), .clk(in_3), .clr(in_4));
  Multiplexer #(.select(5), .width(32), .enable("false")) multiplexer_1 (
    .in0(RAM_0), .in1(RAM_1), .in2(RAM_2), .in3(RAM_3), .in4(RAM_4), .in5(RAM_5), .in6(RAM_6), .in7(RAM_7),
    .in8(RAM_8), .in9(RAM_9), .in10(RAM_10), .in11(RAM_11), .in12(RAM_12), .in13(RAM_13), .in14(RAM_14),
    .in15(RAM_15), .in16(RAM_16), .in17(RAM_17), .in18(RAM_18), .in19(RAM_19), .in20(RAM_20), .in21(RAM_21),
    .in22(RAM_22), .in23(RAM_23), .in24(RAM_24), .in25(RAM_25), .in26(RAM_26), .in27(RAM_27), .in28(RAM_28),
    .in29(RAM_29), .in30(RAM_30), .in31(RAM_31), .out(out_6), .sel(in_2));

  // Other names for the same wires on the sheet: adr[4:0] = in_2; clk = in_3; R_W = in_5; RAM_In[31:0] = in_1;
  //   RAM_Out[31:0] = out_6; Reset = in_4

  // Notes on the sheet:
  //   Entradas
  //   Registros
  //   Salidas
endmodule
